// Logisim project CircuitoExamen1MarcoFerraroGabrielRevillat.circ as structural Verilog: 2 circuits, main circuit main
module main (
  input  [15:0] in_1,
  output [7:0] Byte
);

  wire clock_1_out, demultiplexer_1_out0, demultiplexer_1_out1, demultiplexer_1_out2, demultiplexer_1_out3,
       demultiplexer_1_out4, demultiplexer_1_out5, demultiplexer_1_out6, demultiplexer_1_out7,
       demultiplexer_1_out8, demultiplexer_1_out9, demultiplexer_1_out10, demultiplexer_1_out11,
       demultiplexer_1_out12, demultiplexer_1_out13, demultiplexer_1_out14, demultiplexer_1_out15;
  wire [31:0] Cache_Line_data_output, cachememory_1_data_output, cachememory_2_data_output,
       cachememory_3_data_output, cachememory_4_data_output, cachememory_5_data_output,
       cachememory_6_data_output, cachememory_7_data_output, cachememory_8_data_output,
       cachememory_9_data_output, cachememory_10_data_output, cachememory_11_data_output,
       cachememory_12_data_output, cachememory_13_data_output, cachememory_14_data_output,
       cachememory_15_data_output, multiplexer_1_out, rom_1_data;

  ROM #(.addrWidth(16), .dataWidth(32)) rom_1 (.addr(in_1), .data(rom_1_data));  // open: sel
  Clock clock_1 (.out(clock_1_out));
  Demultiplexer #(.select(4), .enable("false")) demultiplexer_1 (
    .out0(demultiplexer_1_out0), .out1(demultiplexer_1_out1), .out2(demultiplexer_1_out2),
    .out3(demultiplexer_1_out3), .out4(demultiplexer_1_out4), .out5(demultiplexer_1_out5),
    .out6(demultiplexer_1_out6), .out7(demultiplexer_1_out7), .out8(demultiplexer_1_out8),
    .out9(demultiplexer_1_out9), .out10(demultiplexer_1_out10), .out11(demultiplexer_1_out11),
    .out12(demultiplexer_1_out12), .out13(demultiplexer_1_out13), .out14(demultiplexer_1_out14),
    .out15(demultiplexer_1_out15), .in(clock_1_out), .sel(in_1[13:10]));
  cacheMemory Cache_Line (
    .Tag(in_1[9:0]), .Clock(demultiplexer_1_out0), .Data_In(rom_1_data), .Data_Output(Cache_Line_data_output));  // open: Hit
  cacheMemory cachememory_1 (
    .Tag(in_1[9:0]), .Clock(demultiplexer_1_out1), .Data_In(rom_1_data),
    .Data_Output(cachememory_1_data_output));  // open: Hit
  cacheMemory cachememory_2 (
    .Tag(in_1[9:0]), .Clock(demultiplexer_1_out2), .Data_In(rom_1_data),
    .Data_Output(cachememory_2_data_output));  // open: Hit
  cacheMemory cachememory_3 (
    .Tag(in_1[9:0]), .Clock(demultiplexer_1_out3), .Data_In(rom_1_data),
    .Data_Output(cachememory_3_data_output));  // open: Hit
  cacheMemory cachememory_4 (
    .Tag(in_1[9:0]), .Clock(demultiplexer_1_out4), .Data_In(rom_1_data),
    .Data_Output(cachememory_4_data_output));  // open: Hit
  cacheMemory cachememory_5 (
    .Tag(in_1[9:0]), .Clock(demultiplexer_1_out5), .Data_In(rom_1_data),
    .Data_Output(cachememory_5_data_output));  // open: Hit
  cacheMemory cachememory_6 (
    .Tag(in_1[9:0]), .Clock(demultiplexer_1_out6), .Data_In(rom_1_data),
    .Data_Output(cachememory_6_data_output));  // open: Hit
  cacheMemory cachememory_7 (
    .Tag(in_1[9:0]), .Clock(demultiplexer_1_out7), .Data_In(rom_1_data),
    .Data_Output(cachememory_7_data_output));  // open: Hit
  cacheMemory cachememory_8 (
    .Tag(in_1[9:0]), .Clock(demultiplexer_1_out8), .Data_In(rom_1_data),
    .Data_Output(cachememory_8_data_output));  // open: Hit
  cacheMemory cachememory_9 (
    .Tag(in_1[9:0]), .Clock(demultiplexer_1_out9), .Data_In(rom_1_data),
    .Data_Output(cachememory_9_data_output));  // open: Hit
  cacheMemory cachememory_10 (
    .Tag(in_1[9:0]), .Clock(demultiplexer_1_out10), .Data_In(rom_1_data),
    .Data_Output(cachememory_10_data_output));  // open: Hit
  cacheMemory cachememory_11 (
    .Tag(in_1[9:0]), .Clock(demultiplexer_1_out11), .Data_In(rom_1_data),
    .Data_Output(cachememory_11_data_output));  // open: Hit
  cacheMemory cachememory_12 (
    .Tag(in_1[9:0]), .Clock(demultiplexer_1_out12), .Data_In(rom_1_data),
    .Data_Output(cachememory_12_data_output));  // open: Hit
  cacheMemory cachememory_13 (
    .Tag(in_1[9:0]), .Clock(demultiplexer_1_out13), .Data_In(rom_1_data),
    .Data_Output(cachememory_13_data_output));  // open: Hit
  cacheMemory cachememory_14 (
    .Tag(in_1[9:0]), .Clock(demultiplexer_1_out14), .Data_In(rom_1_data),
    .Data_Output(cachememory_14_data_output));  // open: Hit
  cacheMemory cachememory_15 (
    .Tag(in_1[9:0]), .Clock(demultiplexer_1_out15), .Data_In(rom_1_data),
    .Data_Output(cachememory_15_data_output));  // open: Hit
  Multiplexer #(.select(4), .width(32), .enable("false")) multiplexer_1 (
    .in0(Cache_Line_data_output), .in1(cachememory_1_data_output), .in2(cachememory_2_data_output),
    .in3(cachememory_3_data_output), .in4(cachememory_4_data_output), .in5(cachememory_5_data_output),
    .in6(cachememory_6_data_output), .in7(cachememory_7_data_output), .in8(cachememory_8_data_output),
    .in9(cachememory_9_data_output), .in10(cachememory_10_data_output), .in11(cachememory_11_data_output),
    .in12(cachememory_12_data_output), .in13(cachememory_13_data_output), .in14(cachememory_14_data_output),
    .in15(cachememory_15_data_output), .out(multiplexer_1_out), .sel(in_1[13:10]));
  Multiplexer #(.select(2), .width(8), .enable("false")) multiplexer_2 (
    .in0(multiplexer_1_out[7:0]), .in1(multiplexer_1_out[15:8]), .in2(multiplexer_1_out[23:16]),
    .in3(multiplexer_1_out[31:24]), .out(Byte), .sel(in_1[15:14]));

  // Notes on the sheet:
  //   contents of rom_1 (hex, n*v repeats v):
  //   77854545 54565353 42455643 23446567 63454234 57454679 23435579 23359632 204*0 32445567 86634535
  //   56342342 56545234 45566343 54365443 45435343 23434567 27544*0 77854545 54565353 42455643 23446567
  //   63454234 57454679 23435579 23359632
endmodule

module cacheMemory (
  input  [9:0] Tag,
  input  Clock,
  input  [31:0] Data_In,
  output Hit,
  output [31:0] Data_Output
);

  wire comparator_1_eq, comparator_2_eq, counter_1_q, not_1_out, not_2_out;
  wire [9:0] demultiplexer_1_out0, demultiplexer_1_out1, Tag_Block_1_q, Tag_Block_2_q;
  wire [31:0] Data_Block_1_q, Data_Block_2_q, demultiplexer_2_out0, demultiplexer_2_out1;

  Clock Clock_Test ();  // open: out
  Demultiplexer #(.width(10), .enable("false")) demultiplexer_1 (
    .out0(demultiplexer_1_out0), .out1(demultiplexer_1_out1), .in(Tag), .sel(counter_1_q));
  Counter #(.width(1), .max('h1), .ongoal("continue")) counter_1 (
    .count(not_2_out), .Q(counter_1_q), .clk(not_2_out));  // open: load, D, carry, clr
  Demultiplexer #(.width(32), .enable("false")) demultiplexer_2 (
    .out0(demultiplexer_2_out0), .out1(demultiplexer_2_out1), .in(Data_In), .sel(counter_1_q));
  not not_1 (not_1_out, counter_1_q);
  Register #(.width(10)) Tag_Block_1 (
    .D(demultiplexer_1_out0), .en(not_1_out), .Q(Tag_Block_1_q), .clk(Clock));  // open: clr
  Register #(.width(10)) Tag_Block_2 (
    .D(demultiplexer_1_out1), .en(counter_1_q), .Q(Tag_Block_2_q), .clk(Clock));  // open: clr
  Register #(.width(32)) Data_Block_1 (
    .D(demultiplexer_2_out0), .en(not_1_out), .Q(Data_Block_1_q), .clk(Clock));  // open: clr
  Register #(.width(32)) Data_Block_2 (
    .D(demultiplexer_2_out1), .en(counter_1_q), .Q(Data_Block_2_q), .clk(Clock));  // open: clr
  Comparator #(.width(10)) comparator_1 (.a(Tag), .b(Tag_Block_1_q), .eq(comparator_1_eq));  // open: gt, lt
  Comparator #(.width(10)) comparator_2 (.a(Tag), .b(Tag_Block_2_q), .eq(comparator_2_eq));  // open: gt, lt
  Multiplexer #(.width(32), .enable("false")) multiplexer_1 (
    .in0(Data_Block_1_q), .in1(Data_Block_2_q), .out(Data_Output), .sel(counter_1_q));
  or or_1 (Hit, comparator_1_eq, comparator_2_eq);
  not not_2 (not_2_out, Hit);
endmodule
