// Logisim project Entregable2.circ as structural Verilog: 2 circuits, main circuit main
module main (
);

  cacheMemory Cache_Line ();  // open: Tag, Data_In, Clock, Hit, Data_Output
endmodule

module cacheMemory (
  input  [9:0] Tag,
  input  [31:0] Data_In,
  input  Clock,
  output Hit,
  output [31:0] Data_Output
);

  wire clock_1_out, comparator_1_eq, comparator_2_eq, counter_1_q, not_1_out, not_2_out;
  wire [9:0] demultiplexer_1_out0, demultiplexer_1_out1, Tag_Block_1_q, Tag_Block_2_q;
  wire [31:0] Data_Block_1_q, Data_Block_2_q, demultiplexer_2_out0, demultiplexer_2_out1;

  Clock clock_1 (.out(clock_1_out));
  Demultiplexer #(.width(10), .enable("false")) demultiplexer_1 (
    .out0(demultiplexer_1_out0), .out1(demultiplexer_1_out1), .in(Tag), .sel(counter_1_q));
  Counter #(.width(1), .max('h1), .ongoal("continue")) counter_1 (
    .count(not_2_out), .Q(counter_1_q), .clk(not_2_out));  // open: load, D, carry, clr
  Demultiplexer #(.width(32), .enable("false")) demultiplexer_2 (
    .out0(demultiplexer_2_out0), .out1(demultiplexer_2_out1), .in(Data_In), .sel(counter_1_q));
  not not_1 (not_1_out, counter_1_q);
  Register #(.width(10)) Tag_Block_1 (
    .D(demultiplexer_1_out0), .en(not_1_out), .Q(Tag_Block_1_q), .clk(clock_1_out));  // open: clr
  Register #(.width(10)) Tag_Block_2 (
    .D(demultiplexer_1_out1), .en(counter_1_q), .Q(Tag_Block_2_q), .clk(clock_1_out));  // open: clr
  Register #(.width(32)) Data_Block_1 (
    .D(demultiplexer_2_out0), .en(not_1_out), .Q(Data_Block_1_q), .clk(clock_1_out));  // open: clr
  Register #(.width(32)) Data_Block_2 (
    .D(demultiplexer_2_out1), .en(counter_1_q), .Q(Data_Block_2_q), .clk(clock_1_out));  // open: clr
  Comparator #(.width(10)) comparator_1 (.a(Tag), .b(Tag_Block_1_q), .eq(comparator_1_eq));  // open: gt, lt
  Comparator #(.width(10)) comparator_2 (.a(Tag), .b(Tag_Block_2_q), .eq(comparator_2_eq));  // open: gt, lt
  Multiplexer #(.width(32), .enable("false")) multiplexer_1 (
    .in0(Data_Block_1_q), .in1(Data_Block_2_q), .out(Data_Output), .sel(counter_1_q));
  or or_1 (Hit, comparator_1_eq, comparator_2_eq);
  not not_2 (not_2_out, Hit);
endmodule
