// Logisim project CPU.circ as structural Verilog: 15 circuits, main circuit main
module main (
  output out_1,
  output out_2,
  output out_3,
  output out_4,
  output [31:0] out_5,
  output [4:0] out_6,
  output out_7,
  output out_8
);

  wire alu_1_equal, controlunit_1_p6, controlunit_1_p8, controlunit_1_p10, controlunit_1_p12,
       controlunit_1_p16, controlunit_1_p17, controlunit_1_p18, controlunit_1_p19, controlunit_1_p20,
       ex_mem_1_equal_mem, ex_mem_1_mem_branch, ex_mem_1_mem_memread, ex_mem_1_mem_memtoreg,
       ex_mem_1_mem_memwrite, EX_MEM_RegWrite, id_ex_1_alusrc_ex, id_ex_1_isbranch_ex, id_ex_1_memread_ex,
       id_ex_1_memtoreg_ex, id_ex_1_memwrite_ex, id_ex_1_regdst_ex, id_ex_1_regwrite_ex,
       mem_wb_1_memtoreg_wb, PC_SELECTOR;
  wire [1:0] Fw_A, Fw_B, PC_SELECTOR_2;
  wire [3:0] controlunit_1_p9, id_ex_1_aluop_ex;
  wire [4:0] EX_MEM_rd, id_ex_1_writereg1_ex, id_ex_1_writereg2_ex, multiplexer_4_out;
  wire [31:0] adder_2_out, alu_1_result, alu_1_result_2, ALUResult, bit_extender_1_out, bit_extender_2_out,
       datamemory_1_readdata, ex_mem_1_rt_mem, id_ex_1_crs_ex, id_ex_1_crt_ex, id_ex_1_imm_ex,
       id_ex_1_pc_4_ex, id_ex_1_shamt_ex, ID_PC_4, if_id_1_id_inst, Instruction_Memory_data,
       mem_wb_1_aluresult_wb, mem_wb_1_readdata_wb, multiplexer_1_out, multiplexer_3_out, multiplexer_5_out,
       multiplexer_6_out, multiplexer_7_out, n32bit_registerfile_1_drs, n32bit_registerfile_1_drt, PC_4,
       PC_BRANCH, PC_J, PC_JAL, Program_Counter_q, shifter_1_out;

  Clock clock_1 (.out(out_7));
  Multiplexer #(.width(32), .enable("false")) multiplexer_1 (
    .in0(PC_4), .in1(PC_BRANCH), .out(multiplexer_1_out), .sel(PC_SELECTOR));
  Register #(.width(32), .Select("low")) Program_Counter (
    .D(multiplexer_1_out), .Q(Program_Counter_q), .clk(out_7));  // open: en, clr
  Multiplexer #(.select(2), .width(32), .enable("false")) multiplexer_2 (
    .in0(PC_4), .in1(PC_BRANCH), .in2(PC_J), .in3(PC_JAL), .sel(PC_SELECTOR_2));  // open: out
  Adder #(.width(32)) adder_1 (.a(Program_Counter_q), .b(32'h4), .out(PC_4));  // open: cin, cout
  ROM #(.addrWidth(9), .dataWidth(32), .Select("low")) Instruction_Memory (
    .addr(Program_Counter_q[8:0]), .data(Instruction_Memory_data));
  // Probe on PC_4
  IF_ID if_id_1 (
    .En(1'b1), .IF_Inst(Instruction_Memory_data), .IF_PC_4(PC_4), .CLK(out_7), .ID_Inst(if_id_1_id_inst),
    .ID_PC_4(ID_PC_4), .Clear(1'b0));
  // Probe on ID_PC_4
  // ControlUnit controlunit_1: pin names not known; wires that end beside it: if_id_1_id_inst[5:0], if_id_1_id_inst[31:26], 1'b1, out_7, 1'b0, controlunit_1_p6, controlunit_1_p6, controlunit_1_p8, controlunit_1_p9, controlunit_1_p10, out_2, controlunit_1_p12, out_3, controlunit_1_p8, out_1, controlunit_1_p16, controlunit_1_p17, controlunit_1_p18, controlunit_1_p19, controlunit_1_p20
  _32Bit_RegisterFile u_32bit_registerfile_1 (
    .clock(out_7), .rs(if_id_1_id_inst[25:21]), .rt(if_id_1_id_inst[20:16]), .rd(out_6), .RegWrite(out_4),
    .drs(n32bit_registerfile_1_drs), .drt(n32bit_registerfile_1_drt), .WriteData(out_5));
  assign bit_extender_1_out = {{16{if_id_1_id_inst[15]}}, if_id_1_id_inst[15:0]};  // Bit_Extender bit_extender_1
  assign bit_extender_2_out = {{27{1'b0}}, if_id_1_id_inst[10:6]};  // Bit_Extender bit_extender_2
  ID_EX id_ex_1 (
    .Clock(out_7), .Clear(1'b0), .Enable(1'b1), .PC_4_ID(ID_PC_4), .PC_4_EX(id_ex_1_pc_4_ex),
    .Imm_ID(bit_extender_1_out), .Imm_EX(id_ex_1_imm_ex), .Shamt_ID(bit_extender_2_out),
    .Shamt_EX(id_ex_1_shamt_ex), .CRS_ID(n32bit_registerfile_1_drs), .CRS_EX(id_ex_1_crs_ex),
    .CRT_ID(n32bit_registerfile_1_drt), .CRT_EX(id_ex_1_crt_ex), .WriteReg1_ID(if_id_1_id_inst[20:16]),
    .WriteReg1_EX(id_ex_1_writereg1_ex), .ALUOp_EX(id_ex_1_aluop_ex), .RegWrite_ID(controlunit_1_p10),
    .RegWrite_EX(id_ex_1_regwrite_ex), .MemToReg_ID(controlunit_1_p12), .MemToReg_EX(id_ex_1_memtoreg_ex),
    .IsBranch_ID(controlunit_1_p16), .IsBranch_EX(id_ex_1_isbranch_ex), .MemRead_ID(controlunit_1_p17),
    .MemRead_EX(id_ex_1_memread_ex), .MemWrite_ID(controlunit_1_p18), .MemWrite_EX(id_ex_1_memwrite_ex),
    .ALUSrc_EX(id_ex_1_alusrc_ex), .ALUSrc_ID(controlunit_1_p19), .ALUOp_ID(controlunit_1_p9),
    .WriteReg2_ID(if_id_1_id_inst[15:11]), .WriteReg2_EX(id_ex_1_writereg2_ex),
    .RegDst_ID(controlunit_1_p20), .RegDst_EX(id_ex_1_regdst_ex));
  Multiplexer #(.width(32), .enable("false")) multiplexer_3 (
    .in0(id_ex_1_crt_ex), .in1(id_ex_1_shamt_ex), .out(multiplexer_3_out), .sel(id_ex_1_alusrc_ex));
  Multiplexer #(.width(5), .enable("false")) multiplexer_4 (
    .in0(id_ex_1_writereg1_ex), .in1(id_ex_1_writereg2_ex), .out(multiplexer_4_out), .sel(id_ex_1_regdst_ex));
  ForwardingUnit forwardingunit_1 (
    .ID_EX_rs(if_id_1_id_inst[25:21]), .EX_MEM_rd(EX_MEM_rd), .EX_MEM_RegWrite(EX_MEM_RegWrite),
    .ID_EX_rt(if_id_1_id_inst[20:16]), .MEM_WB_rd(out_6), .MEM_WB_RegWrite(out_4), .ForwardA(Fw_A),
    .ForwardB(Fw_B));
  Multiplexer #(.width(32), .enable("false")) multiplexer_5 (
    .in0(multiplexer_3_out), .in1(id_ex_1_imm_ex), .out(multiplexer_5_out), .sel(id_ex_1_alusrc_ex));
  Multiplexer #(.select(2), .width(32), .enable("false")) multiplexer_6 (
    .in0(id_ex_1_crs_ex), .in1(out_5), .in2(ALUResult), .out(multiplexer_6_out), .sel(Fw_A));  // open: in3
  ALU alu_1 (
    .A(multiplexer_6_out), .B(multiplexer_7_out), .AluOP(id_ex_1_aluop_ex), .Equal(alu_1_equal),
    .Result(alu_1_result), .Result_2(alu_1_result_2));  // open: Signed_Overflow, UnSigned_Overflow
  Multiplexer #(.select(2), .width(32), .enable("false")) multiplexer_7 (
    .in0(multiplexer_5_out), .in1(out_5), .in2(ALUResult), .out(multiplexer_7_out), .sel(Fw_B));  // open: in3
  Shifter #(.width(32)) shifter_1 (.in(id_ex_1_imm_ex), .\dist (5'b00010), .out(shifter_1_out));
  Adder #(.width(32)) adder_2 (.a(id_ex_1_pc_4_ex), .b(shifter_1_out), .out(adder_2_out));  // open: cin, cout
  EX_MEM ex_mem_1 (
    .Clock(out_7), .EX_Clear(1'b0), .EX_Enable(1'b1), .EX_PC(adder_2_out), .EX_ALURes(alu_1_result),
    .EX_ALURes2(alu_1_result_2), .EX_rd(multiplexer_4_out), .EX_RegWrite(id_ex_1_regwrite_ex),
    .EX_MemToReg(id_ex_1_memtoreg_ex), .EX_MemRead(id_ex_1_isbranch_ex), .EX_MemWrite(id_ex_1_memread_ex),
    .EX_Branch(id_ex_1_memwrite_ex), .MEM_PC(PC_BRANCH), .MEM_ALURes(ALUResult), .MEM_rd(EX_MEM_rd),
    .MEM_RegWrite(EX_MEM_RegWrite), .MEM_MemToReg(ex_mem_1_mem_memtoreg), .MEM_MemRead(ex_mem_1_mem_memread),
    .MEM_MemWrite(ex_mem_1_mem_memwrite), .MEM_Branch(ex_mem_1_mem_branch), .RT_EX(id_ex_1_crt_ex),
    .RT_MEM(ex_mem_1_rt_mem), .Equal_EX(alu_1_equal), .Equal_MEM(ex_mem_1_equal_mem));  // open: MEM_ALURes2
  and and_1 (PC_SELECTOR, ex_mem_1_mem_branch, ex_mem_1_equal_mem);
  DataMemory datamemory_1 (
    .Address(ALUResult), .WriteData(ex_mem_1_rt_mem), .MemRead(ex_mem_1_mem_memread),
    .MemWrite(ex_mem_1_mem_memwrite), .Clock(out_7), .ReadData(datamemory_1_readdata));
  MEM_WB mem_wb_1 (
    .Clock(out_7), .EX_Clear(1'b0), .EX_Enable(1'b1), .ReadData_MEM(datamemory_1_readdata),
    .ALUResult_MEM(ALUResult), .MemToReg_MEM(ex_mem_1_mem_memtoreg), .ReadData_WB(mem_wb_1_readdata_wb),
    .ALUResult_WB(mem_wb_1_aluresult_wb), .MemToReg_WB(mem_wb_1_memtoreg_wb), .RegWrite_MEM(EX_MEM_RegWrite),
    .RegWrite_WB(out_4), .rd_MEM(EX_MEM_rd), .rd_WB(out_6));
  Multiplexer #(.width(32), .enable("false")) multiplexer_8 (
    .in0(mem_wb_1_readdata_wb), .in1(mem_wb_1_aluresult_wb), .out(out_5), .sel(mem_wb_1_memtoreg_wb));

  assign out_8 = 1'b0;

  // Other names for the same wires on the sheet: Clock = out_7; isJR = out_2; isJump = out_1; isSysCall = out_3;
  //   RegWrite = out_4; WriteData[31:0] = out_5; WriteReg[4:0] = out_6

  // Notes on the sheet:
  //   Estudiantes: Marco Ferraro, Gabriel Revillat
  //   Proyecto Arquitectura de Computadores
  //   Updated PC
  //   Flag Values
  //   Register Values
endmodule

// Reg File
module _32Bit_RegisterFile (
  input  clock,
  input  [4:0] rs,
  input  [4:0] rt,
  input  [4:0] rd,
  input  RegWrite,
  input  [31:0] WriteData,
  output [31:0] drs,
  output [31:0] drt
);

  wire demultiplexer_1_out0, demultiplexer_1_out1, demultiplexer_1_out2, demultiplexer_1_out3,
       demultiplexer_1_out4, demultiplexer_1_out5, demultiplexer_1_out6, demultiplexer_1_out7,
       demultiplexer_1_out8, demultiplexer_1_out9, demultiplexer_1_out10, demultiplexer_1_out11,
       demultiplexer_1_out12, demultiplexer_1_out13, demultiplexer_1_out14, demultiplexer_1_out15,
       demultiplexer_1_out16, demultiplexer_1_out17, demultiplexer_1_out18, demultiplexer_1_out19,
       demultiplexer_1_out20, demultiplexer_1_out21, demultiplexer_1_out22, demultiplexer_1_out23,
       demultiplexer_1_out24, demultiplexer_1_out25, demultiplexer_1_out26, demultiplexer_1_out27,
       demultiplexer_1_out28, demultiplexer_1_out29, demultiplexer_1_out30, demultiplexer_1_out31;
  wire [31:0] register_1_q, register_2_q, register_3_q, register_4_q, register_5_q, register_6_q,
       register_7_q, register_8_q, register_9_q, register_10_q, register_11_q, register_12_q, register_13_q,
       register_14_q, register_15_q, register_16_q, register_17_q, register_18_q, register_20_q,
       register_21_q, register_22_q, register_23_q, register_24_q, register_25_q, register_26_q,
       register_27_q, register_28_q, register_29_q, register_30_q, register_31_q, register_32_q;

  Demultiplexer #(.select(5), .enable("false")) demultiplexer_1 (
    .out0(demultiplexer_1_out0), .out1(demultiplexer_1_out1), .out2(demultiplexer_1_out2),
    .out3(demultiplexer_1_out3), .out4(demultiplexer_1_out4), .out5(demultiplexer_1_out5),
    .out6(demultiplexer_1_out6), .out7(demultiplexer_1_out7), .out8(demultiplexer_1_out8),
    .out9(demultiplexer_1_out9), .out10(demultiplexer_1_out10), .out11(demultiplexer_1_out11),
    .out12(demultiplexer_1_out12), .out13(demultiplexer_1_out13), .out14(demultiplexer_1_out14),
    .out15(demultiplexer_1_out15), .out16(demultiplexer_1_out16), .out17(demultiplexer_1_out17),
    .out18(demultiplexer_1_out18), .out19(demultiplexer_1_out19), .out20(demultiplexer_1_out20),
    .out21(demultiplexer_1_out21), .out22(demultiplexer_1_out22), .out23(demultiplexer_1_out23),
    .out24(demultiplexer_1_out24), .out25(demultiplexer_1_out25), .out26(demultiplexer_1_out26),
    .out27(demultiplexer_1_out27), .out28(demultiplexer_1_out28), .out29(demultiplexer_1_out29),
    .out30(demultiplexer_1_out30), .out31(demultiplexer_1_out31), .in(RegWrite), .sel(rd));
  Register #(.width(32), .Select("low")) register_1 (.D(WriteData), .en(1'b0), .Q(register_1_q));  // open: clk, clr
  Register #(.width(32), .Select("low")) register_2 (
    .D(WriteData), .en(demultiplexer_1_out8), .Q(register_2_q), .clk(clock), .clr(clock));
  Register #(.width(32), .Select("low")) register_3 (
    .D(WriteData), .en(demultiplexer_1_out16), .Q(register_3_q), .clk(clock));  // open: clr
  Register #(.width(32), .Select("low")) register_4 (
    .D(WriteData), .en(demultiplexer_1_out24), .Q(register_4_q));  // open: clk, clr
  Register #(.width(32), .Select("low")) register_5 (
    .D(WriteData), .en(demultiplexer_1_out1), .Q(register_5_q), .clk(clock));  // open: clr
  Register #(.width(32), .Select("low")) register_6 (
    .D(WriteData), .en(demultiplexer_1_out9), .Q(register_6_q), .clk(clock));  // open: clr
  Register #(.width(32), .Select("low")) register_7 (
    .D(WriteData), .en(demultiplexer_1_out17), .Q(register_7_q), .clk(clock));  // open: clr
  Register #(.width(32), .Select("low")) register_8 (
    .D(WriteData), .en(demultiplexer_1_out25), .Q(register_8_q), .clk(clock));  // open: clr
  Register #(.width(32), .Select("low")) register_9 (
    .D(WriteData), .en(demultiplexer_1_out2), .Q(register_9_q), .clk(clock));  // open: clr
  Register #(.width(32), .Select("low")) register_10 (
    .D(WriteData), .en(demultiplexer_1_out10), .Q(register_10_q), .clk(clock));  // open: clr
  Register #(.width(32), .Select("low")) register_11 (
    .D(WriteData), .en(demultiplexer_1_out18), .Q(register_11_q), .clk(clock));  // open: clr
  Register #(.width(32), .Select("low")) register_12 (
    .D(WriteData), .en(demultiplexer_1_out26), .Q(register_12_q));  // open: clk, clr
  Register #(.width(32), .Select("low")) register_13 (
    .D(WriteData), .en(demultiplexer_1_out3), .Q(register_13_q), .clk(clock));  // open: clr
  Register #(.width(32), .Select("low")) register_14 (
    .D(WriteData), .en(demultiplexer_1_out11), .Q(register_14_q), .clk(clock));  // open: clr
  Register #(.width(32), .Select("low")) register_15 (
    .D(WriteData), .en(demultiplexer_1_out19), .Q(register_15_q), .clk(clock));  // open: clr
  Register #(.width(32), .Select("low")) register_16 (
    .D(WriteData), .en(demultiplexer_1_out27), .Q(register_16_q));  // open: clk, clr
  Register #(.width(32), .Select("low")) register_17 (
    .D(WriteData), .en(demultiplexer_1_out4), .Q(register_17_q), .clk(clock));  // open: clr
  Register #(.width(32), .Select("low")) register_18 (
    .D(WriteData), .en(demultiplexer_1_out12), .Q(register_18_q), .clk(clock));  // open: clr
  Register #(.width(32), .Select("low")) register_19 (
    .D(WriteData), .en(demultiplexer_1_out20), .Q(register_15_q), .clk(clock));  // open: clr
  Register #(.width(32), .Select("low")) register_20 (
    .D(WriteData), .en(demultiplexer_1_out28), .Q(register_20_q));  // open: clk, clr
  Register #(.width(32), .Select("low")) register_21 (
    .D(WriteData), .en(demultiplexer_1_out5), .Q(register_21_q), .clk(clock));  // open: clr
  Register #(.width(32), .Select("low")) register_22 (
    .D(WriteData), .en(demultiplexer_1_out13), .Q(register_22_q), .clk(clock));  // open: clr
  Register #(.width(32), .Select("low")) register_23 (
    .D(WriteData), .en(demultiplexer_1_out21), .Q(register_23_q), .clk(clock));  // open: clr
  Register #(.width(32), .Select("low")) register_24 (
    .D(WriteData), .en(demultiplexer_1_out29), .Q(register_24_q));  // open: clk, clr
  Register #(.width(32), .Select("low")) register_25 (
    .D(WriteData), .en(demultiplexer_1_out6), .Q(register_25_q), .clk(clock));  // open: clr
  Register #(.width(32), .Select("low")) register_26 (
    .D(WriteData), .en(demultiplexer_1_out14), .Q(register_26_q), .clk(clock));  // open: clr
  Register #(.width(32), .Select("low")) register_27 (
    .D(WriteData), .en(demultiplexer_1_out22), .Q(register_27_q), .clk(clock));  // open: clr
  Register #(.width(32), .Select("low")) register_28 (
    .D(WriteData), .en(demultiplexer_1_out30), .Q(register_28_q));  // open: clk, clr
  Register #(.width(32), .Select("low")) register_29 (
    .D(WriteData), .en(demultiplexer_1_out7), .Q(register_29_q), .clk(clock));  // open: clr
  Register #(.width(32), .Select("low")) register_30 (
    .D(WriteData), .en(demultiplexer_1_out15), .Q(register_30_q), .clk(clock));  // open: clr
  Register #(.width(32), .Select("low")) register_31 (
    .D(WriteData), .en(demultiplexer_1_out23), .Q(register_31_q), .clk(clock));  // open: clr
  Register #(.width(32), .Select("low")) register_32 (
    .D(WriteData), .en(demultiplexer_1_out31), .Q(register_32_q));  // open: clk, clr
  Multiplexer #(.select(5), .width(32), .enable("false")) multiplexer_1 (
    .in0(register_1_q), .in1(register_5_q), .in2(register_9_q), .in3(register_13_q), .in4(register_17_q),
    .in5(register_21_q), .in6(register_25_q), .in7(register_29_q), .in8(register_2_q), .in9(register_6_q),
    .in10(register_10_q), .in11(register_14_q), .in12(register_18_q), .in13(register_22_q),
    .in14(register_26_q), .in15(register_30_q), .in16(register_3_q), .in17(register_7_q),
    .in18(register_11_q), .in19(register_15_q), .in20(register_15_q), .in21(register_23_q),
    .in22(register_27_q), .in23(register_31_q), .in24(register_4_q), .in25(register_8_q),
    .in26(register_12_q), .in27(register_16_q), .in28(register_20_q), .in29(register_24_q),
    .in30(register_28_q), .in31(register_32_q), .out(drs), .sel(rs));
  Multiplexer #(.select(5), .width(32), .enable("false")) multiplexer_2 (
    .in0(register_1_q), .in1(register_5_q), .in2(register_9_q), .in3(register_13_q), .in4(register_17_q),
    .in5(register_21_q), .in6(register_25_q), .in7(register_29_q), .in8(register_2_q), .in9(register_6_q),
    .in10(register_10_q), .in11(register_14_q), .in12(register_18_q), .in13(register_22_q),
    .in14(register_26_q), .in15(register_30_q), .in16(register_3_q), .in17(register_7_q),
    .in18(register_11_q), .in19(register_15_q), .in20(register_15_q), .in21(register_23_q),
    .in22(register_27_q), .in23(register_31_q), .in24(register_4_q), .in25(register_8_q),
    .in26(register_12_q), .in27(register_16_q), .in28(register_20_q), .in29(register_24_q),
    .in30(register_28_q), .in31(register_32_q), .out(drt), .sel(rt));

  // Notes on the sheet:
  //   Register File
endmodule

module IF_ID (
  input  En,
  input  [31:0] IF_Inst,
  input  [31:0] IF_PC_4,
  input  CLK,
  input  Clear,
  output [31:0] ID_Inst,
  output [31:0] ID_PC_4
);

  Register #(.width(32), .Select("low")) Inst (.D(IF_Inst), .en(En), .Q(ID_Inst), .clk(CLK), .clr(Clear));
  Register #(.width(32), .Select("low")) PC (.D(IF_PC_4), .en(En), .Q(ID_PC_4), .clk(CLK), .clr(Clear));
endmodule

// Control Unit
module ControlUnit (
  input  Clock,
  input  EX_Clear,
  input  EX_Enable,
  input  [5:0] OpCode,
  input  [5:0] Function,
  input  [4:0] rt,
  output RegWrite,
  output MemToReg,
  output MemRead,
  output MemWrite,
  output IsBranch,
  output ALUSrc,
  output RegDst,
  output IsJR,
  output IsJump,
  output IsSysCall,
  output [3:0] ALUOp
);

  wire and_4_out, and_5_out, and_7_out, and_8_out, IsSpecial, JALR_out, not_1_out, Special_2_out, SysCall_out;
  wire [3:0] FunctionDecoder__0, OpDecoder__3;

  and JR (IsJR, ~Function[5], ~Function[4], Function[3], ~Function[2], ~Function[1], ~Function[0]);  // AND_Gate
  and Special (IsSpecial, ~OpCode[5], ~OpCode[4], ~OpCode[3], ~OpCode[2], ~OpCode[1], ~OpCode[0]);  // AND_Gate
  and JALR (JALR_out, ~Function[5], ~Function[4], Function[3], ~Function[2], ~Function[1], Function[0]);  // AND_Gate
  and Special_2 (Special_2_out, ~OpCode[5], ~OpCode[4], ~OpCode[3], ~OpCode[2], ~OpCode[1], ~OpCode[0]);  // AND_Gate
  and SysCall (SysCall_out, ~Function[5], ~Function[4], Function[3], Function[2], ~Function[1], ~Function[0]);  // AND_Gate
  FunctionDecode FunctionDecoder (
    .Function(Function), ._3(FunctionDecoder__0[3]), ._2(FunctionDecoder__0[2]), ._1(FunctionDecoder__0[1]),
    ._0(FunctionDecoder__0[0]));
  OpCodeDecode OpDecoder (
    .OpCode(OpCode), ._0(OpDecoder__3[3]), ._1(OpDecoder__3[2]), ._2(OpDecoder__3[1]), ._3(OpDecoder__3[0]));
  RegWriteDecode RegWriteDecoder (.OpCode(OpCode), .RegWrite(RegWrite));
  and and_1 (MemToReg, OpCode[5], ~OpCode[4], ~OpCode[3], ~OpCode[2], OpCode[1], OpCode[0]);  // AND_Gate
  and and_2 (MemRead, OpCode[5], ~OpCode[4], ~OpCode[3], ~OpCode[2], OpCode[1], OpCode[0]);  // AND_Gate
  and and_3 (MemWrite, OpCode[5], ~OpCode[4], OpCode[3], ~OpCode[2], OpCode[1], OpCode[0]);  // AND_Gate
  and and_4 (and_4_out, ~OpCode[5], ~OpCode[4], ~OpCode[3], OpCode[2], ~OpCode[1], OpCode[0]);  // AND_Gate
  and and_5 (and_5_out, ~OpCode[5], ~OpCode[4], ~OpCode[3], OpCode[2], ~OpCode[1], ~OpCode[0]);  // AND_Gate
  ALUSrcDecode ALUSrcDecoder (.OpCode(OpCode), .ALUSrc(ALUSrc));
  and and_6 (RegDst, ~OpCode[5], ~OpCode[4], ~OpCode[3], ~OpCode[2], ~OpCode[1], ~OpCode[0]);  // AND_Gate
  not not_1 (not_1_out, IsSpecial);
  or or_1 (IsBranch, and_4_out, and_5_out);
  and and_7 (and_7_out, IsJR, IsSpecial);
  and and_8 (and_8_out, IsSpecial, JALR_out);
  and and_9 (IsSysCall, Special_2_out, SysCall_out);
  Multiplexer #(.width(4), .enable("false")) multiplexer_1 (
    .in0(FunctionDecoder__0), .in1(OpDecoder__3), .out(ALUOp), .sel(not_1_out));
  or or_2 (IsJump, and_7_out, and_8_out);

  // Other names for the same wires on the sheet: Clear = EX_Clear; Enable = EX_Enable

  // Notes on the sheet:
  //   Control
  //   Entradas y salidas
  //   WB
  //   MEM
  //   EX
endmodule

module ID_EX (
  input  Clock,
  input  Clear,
  input  Enable,
  input  [31:0] PC_4_ID,
  input  [31:0] CRS_ID,
  input  [31:0] CRT_ID,
  input  [31:0] Imm_ID,
  input  [31:0] Shamt_ID,
  input  [4:0] WriteReg1_ID,
  input  [4:0] WriteReg2_ID,
  input  RegWrite_ID,
  input  MemToReg_ID,
  input  IsBranch_ID,
  input  MemRead_ID,
  input  MemWrite_ID,
  input  ALUSrc_ID,
  input  [3:0] ALUOp_ID,
  input  RegDst_ID,
  output [31:0] PC_4_EX,
  output [31:0] CRS_EX,
  output [31:0] CRT_EX,
  output [31:0] Imm_EX,
  output [31:0] Shamt_EX,
  output [4:0] WriteReg1_EX,
  output [4:0] WriteReg2_EX,
  output RegWrite_EX,
  output MemToReg_EX,
  output IsBranch_EX,
  output MemRead_EX,
  output MemWrite_EX,
  output ALUSrc_EX,
  output [3:0] ALUOp_EX,
  output RegDst_EX
);

  Register #(.width(32), .Select("low")) register_1 (.D(PC_4_ID), .en(Enable), .Q(PC_4_EX), .clk(Clock), .clr(Clear));
  Register #(.width(32), .Select("low")) register_2 (.D(CRS_ID), .en(Enable), .Q(CRS_EX), .clk(Clock), .clr(Clear));
  Register #(.width(32), .Select("low")) register_3 (.D(CRT_ID), .en(Enable), .Q(CRT_EX), .clk(Clock), .clr(Clear));
  Register #(.width(32), .Select("low")) register_4 (.D(Imm_ID), .en(Enable), .Q(Imm_EX), .clk(Clock), .clr(Clear));
  Register #(.width(32), .Select("low")) register_5 (.D(Shamt_ID), .en(Enable), .Q(Shamt_EX), .clk(Clock), .clr(Clear));
  Register #(.width(5), .Select("low")) register_6 (
    .D(WriteReg1_ID), .en(Enable), .Q(WriteReg1_EX), .clk(Clock), .clr(Clear));
  Register #(.width(5), .Select("low")) register_7 (
    .D(WriteReg2_ID), .en(Enable), .Q(WriteReg2_EX), .clk(Clock), .clr(Clear));
  Register #(.width(1), .Select("low")) register_8 (
    .D(RegWrite_ID), .en(Enable), .Q(RegWrite_EX), .clk(Clock), .clr(Clear));
  Register #(.width(1), .Select("low")) register_9 (
    .D(MemToReg_ID), .en(Enable), .Q(MemToReg_EX), .clk(Clock), .clr(Clear));
  Register #(.width(1), .Select("low")) register_10 (
    .D(IsBranch_ID), .en(Enable), .Q(IsBranch_EX), .clk(Clock), .clr(Clear));
  Register #(.width(1), .Select("low")) register_11 (
    .D(MemRead_ID), .en(Enable), .Q(MemRead_EX), .clk(Clock), .clr(Clear));
  Register #(.width(1), .Select("low")) register_12 (
    .D(MemWrite_ID), .en(Enable), .Q(MemWrite_EX), .clk(Clock), .clr(Clear));
  Register #(.width(1), .Select("low")) register_13 (
    .D(ALUSrc_ID), .en(Enable), .Q(ALUSrc_EX), .clk(Clock), .clr(Clear));
  Register #(.width(4), .Select("low")) register_14 (.D(ALUOp_ID), .en(Enable), .Q(ALUOp_EX), .clk(Clock), .clr(Clear));
  Register #(.width(1), .Select("low")) register_15 (
    .D(RegDst_ID), .en(Enable), .Q(RegDst_EX), .clk(Clock), .clr(Clear));

  // Notes on the sheet:
  //   Datapath
  //   Control
  //   WB
  //   MEM
  //   EX
endmodule

module RegWriteDecode (
  input  [5:0] OpCode,
  output RegWrite
);

  wire and_1_out, and_2_out, and_3_out, and_4_out, and_5_out, and_6_out, and_7_out, and_8_out, and_9_out,
       and_10_out;

  and and_1 (and_1_out, ~OpCode[5], ~OpCode[4], ~OpCode[3], ~OpCode[2], ~OpCode[1], ~OpCode[0]);  // AND_Gate
  and and_2 (and_2_out, ~OpCode[5], ~OpCode[4], OpCode[3], ~OpCode[2], ~OpCode[1], ~OpCode[0]);  // AND_Gate
  and and_3 (and_3_out, OpCode[5], ~OpCode[4], ~OpCode[3], ~OpCode[2], OpCode[1], OpCode[0]);  // AND_Gate
  and and_4 (and_4_out, ~OpCode[5], ~OpCode[4], OpCode[3], OpCode[2], ~OpCode[1], ~OpCode[0]);  // AND_Gate
  and and_5 (and_5_out, ~OpCode[5], ~OpCode[4], OpCode[3], OpCode[2], ~OpCode[1], OpCode[0]);  // AND_Gate
  and and_6 (and_6_out, ~OpCode[5], ~OpCode[4], OpCode[3], ~OpCode[2], OpCode[1], ~OpCode[0]);  // AND_Gate
  and and_7 (and_7_out, ~OpCode[5], ~OpCode[4], OpCode[3], ~OpCode[2], ~OpCode[1], OpCode[0]);  // AND_Gate
  and and_8 (and_8_out, ~OpCode[5], ~OpCode[4], OpCode[3], ~OpCode[2], ~OpCode[1], ~OpCode[0]);  // AND_Gate
  and and_9 (and_9_out, ~OpCode[5], ~OpCode[4], ~OpCode[3], ~OpCode[2], OpCode[1], OpCode[0]);  // AND_Gate
  and and_10 (and_10_out, ~OpCode[5], OpCode[4], ~OpCode[3], ~OpCode[2], ~OpCode[1], ~OpCode[0]);  // AND_Gate
  or or_1 (RegWrite, and_1_out, and_2_out, and_3_out, and_4_out, and_5_out, and_6_out, and_7_out, and_8_out, and_9_out, and_10_out);
endmodule

module ALUSrcDecode (
  input  [5:0] OpCode,
  output ALUSrc
);

  wire and_1_out, and_2_out, and_3_out, and_4_out, and_5_out, and_6_out, and_7_out, and_8_out;

  and and_1 (and_1_out, ~OpCode[5], ~OpCode[4], ~OpCode[3], ~OpCode[2], ~OpCode[1], ~OpCode[0]);  // AND_Gate
  and and_2 (and_2_out, OpCode[5], ~OpCode[4], ~OpCode[3], ~OpCode[2], OpCode[1], OpCode[0]);  // AND_Gate
  and and_3 (and_3_out, OpCode[5], ~OpCode[4], OpCode[3], ~OpCode[2], OpCode[1], OpCode[0]);  // AND_Gate
  and and_4 (and_4_out, ~OpCode[5], ~OpCode[4], OpCode[3], OpCode[2], ~OpCode[1], ~OpCode[0]);  // AND_Gate
  and and_5 (and_5_out, ~OpCode[5], ~OpCode[4], OpCode[3], OpCode[2], ~OpCode[1], OpCode[0]);  // AND_Gate
  and and_6 (and_6_out, ~OpCode[5], ~OpCode[4], OpCode[3], ~OpCode[2], OpCode[1], ~OpCode[0]);  // AND_Gate
  and and_7 (and_7_out, ~OpCode[5], ~OpCode[4], OpCode[3], ~OpCode[2], ~OpCode[1], OpCode[0]);  // AND_Gate
  and and_8 (and_8_out, ~OpCode[5], ~OpCode[4], OpCode[3], ~OpCode[2], ~OpCode[1], ~OpCode[0]);  // AND_Gate
  or or_1 (ALUSrc, and_1_out, and_2_out, and_3_out, and_4_out, and_5_out, and_6_out, and_7_out, and_8_out);
endmodule

module FunctionDecode (
  input  [5:0] Function,
  output _0,
  output _1,
  output _2,
  output _3
);

  wire and_1_out, and_2_out, and_3_out, and_4_out, and_5_out, and_6_out, and_7_out, and_8_out, and_9_out,
       and_10_out, and_11_out, and_12_out, and_13_out, and_14_out, and_15_out, and_16_out, and_17_out;

  and and_1 (and_1_out, Function[5], ~Function[4], ~Function[3], Function[2], ~Function[1], Function[0]);  // AND_Gate
  and and_2 (and_2_out, Function[5], ~Function[4], ~Function[3], Function[2], Function[1], Function[0]);  // AND_Gate
  and and_3 (and_3_out, Function[5], ~Function[4], Function[3], ~Function[2], Function[1], ~Function[0]);  // AND_Gate
  and and_4 (and_4_out, Function[5], ~Function[4], Function[3], ~Function[2], Function[1], Function[0]);  // AND_Gate
  and and_5 (and_5_out, Function[5], ~Function[4], ~Function[3], ~Function[2], Function[1], ~Function[0]);  // AND_Gate
  and and_6 (and_6_out, Function[5], ~Function[4], ~Function[3], Function[2], ~Function[1], ~Function[0]);  // AND_Gate
  and and_7 (and_7_out, ~Function[5], ~Function[4], ~Function[3], ~Function[2], Function[1], ~Function[0]);  // AND_Gate
  and and_8 (and_8_out, Function[5], ~Function[4], ~Function[3], Function[2], Function[1], Function[0]);  // AND_Gate
  and and_9 (and_9_out, Function[5], ~Function[4], Function[3], ~Function[2], Function[1], ~Function[0]);  // AND_Gate
  or or_1 (_0, and_1_out, and_2_out, and_3_out, and_4_out);
  or or_2 (_2, and_5_out, and_6_out, and_7_out, and_8_out, and_9_out);
  and and_10 (and_10_out, Function[5], ~Function[4], ~Function[3], ~Function[2], ~Function[1]);  // AND_Gate
  and and_11 (and_11_out, Function[5], ~Function[4], ~Function[3], ~Function[2], ~Function[0]);  // AND_Gate
  and and_12 (and_12_out, Function[5], ~Function[4], ~Function[3], ~Function[1], ~Function[0]);  // AND_Gate
  and and_13 (and_13_out, Function[5], ~Function[4], Function[3], ~Function[2], Function[1], Function[0]);  // AND_Gate
  and and_14 (and_14_out, ~Function[5], ~Function[4], ~Function[3], ~Function[2], Function[1], Function[0]);  // AND_Gate
  and and_15 (and_15_out, Function[5], ~Function[4], ~Function[3], ~Function[2], ~Function[1]);  // AND_Gate
  and and_16 (and_16_out, Function[5], ~Function[4], ~Function[3], ~Function[1], ~Function[0]);  // AND_Gate
  and and_17 (and_17_out, Function[5], ~Function[4], Function[3], ~Function[2], Function[1], ~Function[0]);  // AND_Gate
  or or_3 (_1, and_10_out, and_11_out, and_12_out, and_13_out);
  or or_4 (_3, and_14_out, and_15_out, and_16_out, and_17_out);
endmodule

module OpCodeDecode (
  input  [5:0] OpCode,
  output _0,
  output _1,
  output _2,
  output _3
);

  wire and_1_out, and_2_out, and_3_out, and_4_out, and_5_out, and_6_out, and_7_out, and_8_out, and_9_out,
       and_10_out, and_11_out, and_12_out, and_13_out, and_14_out, and_15_out, and_16_out, and_17_out,
       and_18_out, and_19_out, and_20_out, and_21_out, and_22_out, and_23_out, and_24_out, and_25_out,
       and_26_out, and_27_out, and_28_out, and_29_out;

  and and_1 (and_1_out, ~OpCode[5], ~OpCode[4], OpCode[3], OpCode[2], ~OpCode[1], OpCode[0]);  // AND_Gate
  and and_2 (and_2_out, ~OpCode[5], ~OpCode[4], OpCode[3], ~OpCode[2], OpCode[1], ~OpCode[0]);  // AND_Gate
  and and_3 (and_3_out, ~OpCode[5], ~OpCode[4], ~OpCode[3], ~OpCode[2], ~OpCode[1], ~OpCode[0]);  // AND_Gate
  and and_4 (and_4_out, ~OpCode[5], ~OpCode[4], OpCode[3], ~OpCode[2], ~OpCode[1], ~OpCode[0]);  // AND_Gate
  and and_5 (and_5_out, OpCode[5], ~OpCode[4], ~OpCode[3], ~OpCode[2], OpCode[1], OpCode[0]);  // AND_Gate
  and and_6 (and_6_out, OpCode[5], ~OpCode[4], OpCode[3], ~OpCode[2], OpCode[1], OpCode[0]);  // AND_Gate
  and and_7 (and_7_out, ~OpCode[5], ~OpCode[4], ~OpCode[3], OpCode[2], ~OpCode[1], OpCode[0]);  // AND_Gate
  and and_8 (and_8_out, ~OpCode[5], ~OpCode[4], ~OpCode[3], OpCode[2], ~OpCode[1], ~OpCode[0]);  // AND_Gate
  and and_9 (and_9_out, ~OpCode[5], ~OpCode[4], OpCode[3], OpCode[2], ~OpCode[1], ~OpCode[0]);  // AND_Gate
  and and_10 (and_10_out, ~OpCode[5], ~OpCode[4], OpCode[3], ~OpCode[2], ~OpCode[1], OpCode[0]);  // AND_Gate
  and and_11 (and_11_out, ~OpCode[5], ~OpCode[4], OpCode[3], ~OpCode[2], ~OpCode[1], ~OpCode[0]);  // AND_Gate
  and and_12 (and_12_out, ~OpCode[5], ~OpCode[4], ~OpCode[3], ~OpCode[2], OpCode[1], ~OpCode[0]);  // AND_Gate
  and and_13 (and_13_out, ~OpCode[5], ~OpCode[4], ~OpCode[3], ~OpCode[2], OpCode[1], OpCode[0]);  // AND_Gate
  and and_14 (and_14_out, ~OpCode[5], OpCode[4], ~OpCode[3], ~OpCode[2], ~OpCode[1], ~OpCode[0]);  // AND_Gate
  or or_1 (_0, and_1_out, and_2_out);
  or or_2 (_1, and_3_out, and_4_out, and_5_out, and_6_out, and_7_out, and_8_out, and_9_out, and_10_out, and_11_out, and_12_out, and_13_out, and_14_out);
  and and_15 (and_15_out, ~OpCode[5], ~OpCode[4], OpCode[3], OpCode[2], ~OpCode[1], ~OpCode[0]);  // AND_Gate
  and and_16 (and_16_out, ~OpCode[5], ~OpCode[4], OpCode[3], ~OpCode[2], OpCode[1], ~OpCode[0]);  // AND_Gate
  and and_17 (and_17_out, ~OpCode[5], ~OpCode[4], ~OpCode[3], ~OpCode[2], ~OpCode[1], ~OpCode[0]);  // AND_Gate
  and and_18 (and_18_out, ~OpCode[5], ~OpCode[4], OpCode[3], ~OpCode[2], ~OpCode[1], ~OpCode[0]);  // AND_Gate
  and and_19 (and_19_out, OpCode[5], ~OpCode[4], ~OpCode[3], ~OpCode[2], OpCode[1], OpCode[0]);  // AND_Gate
  and and_20 (and_20_out, OpCode[5], ~OpCode[4], OpCode[3], ~OpCode[2], OpCode[1], OpCode[0]);  // AND_Gate
  and and_21 (and_21_out, ~OpCode[5], ~OpCode[4], ~OpCode[3], OpCode[2], ~OpCode[1], OpCode[0]);  // AND_Gate
  and and_22 (and_22_out, ~OpCode[5], ~OpCode[4], ~OpCode[3], OpCode[2], ~OpCode[1], ~OpCode[0]);  // AND_Gate
  and and_23 (and_23_out, ~OpCode[5], ~OpCode[4], OpCode[3], OpCode[2], ~OpCode[1], ~OpCode[0]);  // AND_Gate
  and and_24 (and_24_out, ~OpCode[5], ~OpCode[4], OpCode[3], ~OpCode[2], OpCode[1], ~OpCode[0]);  // AND_Gate
  and and_25 (and_25_out, ~OpCode[5], ~OpCode[4], OpCode[3], ~OpCode[2], ~OpCode[1], OpCode[0]);  // AND_Gate
  and and_26 (and_26_out, ~OpCode[5], ~OpCode[4], OpCode[3], ~OpCode[2], ~OpCode[1], ~OpCode[0]);  // AND_Gate
  and and_27 (and_27_out, ~OpCode[5], ~OpCode[4], ~OpCode[3], ~OpCode[2], OpCode[1], ~OpCode[0]);  // AND_Gate
  and and_28 (and_28_out, ~OpCode[5], ~OpCode[4], ~OpCode[3], ~OpCode[2], OpCode[1], OpCode[0]);  // AND_Gate
  and and_29 (and_29_out, ~OpCode[5], OpCode[4], ~OpCode[3], ~OpCode[2], ~OpCode[1], ~OpCode[0]);  // AND_Gate
  or or_3 (_2, and_15_out, and_16_out);
  or or_4 (_3, and_17_out, and_18_out, and_19_out, and_20_out, and_21_out, and_22_out, and_23_out, and_24_out, and_25_out, and_26_out, and_27_out, and_28_out, and_29_out);
endmodule

module ALU (
  input  [31:0] A,
  input  [31:0] B,
  input  [3:0] AluOP,
  output Signed_Overflow,
  output UnSigned_Overflow,
  output Equal,
  output [31:0] Result,
  output [31:0] Result_2
);

  wire adder_1_cout, adder_2_cout, and_2_out, cin, comparator_3_gt, comparator_4_gt, subtractor_1_bout,
       xor_2_out;
  wire [0:0] comparator_1_lt, comparator_2_lt;
  wire [6:0] bitadder_1_out;
  wire [30:0] adder_1_out;
  wire [31:0] and_1_out, divider_1_out, divider_1_rem, divider_2_rem, multiplier_1_cout, multiplier_1_out,
       nand_1_out, nor_1_out, shifter_1_out, shifter_2_out, shifter_3_out, subtractor_1_out, xor_1_out;
  wire [31:31] adder_2_out;

  // Probe on A
  // Probe on A
  // Probe on B
  // Probe on B
  Adder #(.width(31)) adder_1 (.a(A[30:0]), .b(B[30:0]), .out(adder_1_out), .cin(cin), .cout(adder_1_cout));
  assign and_1_out = A & B;  // AND_Gate and_1, 32 bits wide
  assign and_1_out = A | B;  // OR_Gate or_1, 32 bits wide
  assign xor_1_out = A ^ B;  // XOR_Gate xor_1, 32 bits wide
  Shifter #(.width(32), .shift("lr")) shifter_1 (.in(A), .\dist (B[4:0]), .out(shifter_1_out));
  Shifter #(.width(32), .shift("ar")) shifter_2 (.in(A), .\dist (B[4:0]), .out(shifter_2_out));
  Comparator #(.width(32)) comparator_1 (.a(A), .b(B), .eq(Equal), .lt(comparator_1_lt[0]));  // open: gt
  Shifter #(.width(32)) shifter_3 (.in(A), .\dist (B[4:0]), .out(shifter_3_out));
  Comparator #(.width(32)) comparator_2 (.a(A), .b(B), .lt(comparator_2_lt[0]));  // open: gt, eq
  Divider #(.width(32)) divider_1 (.a(A), .b(B), .out(divider_1_out), .rem(divider_1_rem));  // open: upper
  Divider #(.width(32)) divider_2 (.a(A), .b(B), .rem(divider_2_rem));  // open: out, upper
  Multiplier #(.width(32)) multiplier_1 (.a(A), .b(B), .out(multiplier_1_out), .cout(multiplier_1_cout));  // open: cin
  Subtractor #(.width(32)) subtractor_1 (.a(A), .b(B), .out(subtractor_1_out), .bout(subtractor_1_bout));  // open: bin
  assign nand_1_out = ~(A & B);  // NAND_Gate nand_1, 32 bits wide
  assign nor_1_out = ~(A | B);  // NOR_Gate nor_1, 32 bits wide
  Adder #(.width(1)) adder_2 (.a(A[31]), .b(B[31]), .out(adder_2_out[31]), .cin(adder_1_cout), .cout(adder_2_cout));
  BitAdder #(.width(32)) bitadder_1 (.in0(A), .in1(B), .out(bitadder_1_out));
  // Probe on AluOP
  // Probe on Result
  // Probe on Result
  xor xor_2 (xor_2_out, adder_1_cout, adder_2_cout);
  Multiplexer #(.select(4), .width(32), .enable("false")) multiplexer_1 (
    .in0({adder_2_out[31], adder_1_out}), .in1(and_1_out), .in2(and_1_out), .in3(xor_1_out),
    .in4(shifter_1_out), .in5(shifter_2_out), .in6({{31{1'b0}}, comparator_1_lt[0]}), .in7(shifter_3_out),
    .in8({{31{1'b0}}, comparator_2_lt[0]}), .in9(divider_1_out), .in10(divider_2_rem),
    .in11(multiplier_1_out), .in12(subtractor_1_out), .in13({{25{1'b0}}, bitadder_1_out}), .in14(nand_1_out),
    .in15(nor_1_out), .out(Result), .sel(AluOP));
  // Probe on Result_2
  Multiplexer #(.select(4), .width(32), .enable("false")) multiplexer_2 (
    .in0({32{1'b0}}), .in1({32{1'b0}}), .in2({32{1'b0}}), .in3({32{1'b0}}), .in4({32{1'b0}}),
    .in5({32{1'b0}}), .in6({32{1'b0}}), .in7({32{1'b0}}), .in8(divider_1_rem), .in9({32{1'b0}}),
    .in10({32{1'b0}}), .in11(multiplier_1_cout), .in12({32{1'b0}}), .in13({32{1'b0}}), .in14({32{1'b0}}),
    .in15({32{1'b0}}), .out(Result_2), .sel(AluOP));
  Comparator #(.width(32)) comparator_3 (.a(multiplier_1_out), .b({32{1'b0}}), .gt(comparator_3_gt));  // open: eq, lt
  Comparator #(.width(32)) comparator_4 (.a(multiplier_1_cout), .b({32{1'b0}}), .gt(comparator_4_gt));  // open: eq, lt
  and and_2 (and_2_out, comparator_3_gt, comparator_4_gt);
  Multiplexer #(.select(4), .enable("false")) multiplexer_3 (
    .in0(adder_2_cout), .in1(1'b0), .in2(1'b0), .in3(1'b0), .in4(1'b0), .in5(1'b0), .in6(1'b0), .in7(1'b0),
    .in8(1'b0), .in9(1'b0), .in10(and_2_out), .in11(1'b0), .in12(1'b0), .in13(1'b0), .in14(1'b0),
    .in15(1'b0), .out(UnSigned_Overflow), .sel(AluOP));
  Multiplexer #(.select(4), .enable("false")) multiplexer_4 (
    .in0(xor_2_out), .in1(1'b0), .in2(1'b0), .in3(1'b0), .in4(1'b0), .in5(1'b0), .in6(1'b0), .in7(1'b0),
    .in8(1'b0), .in9(1'b0), .in10(1'b0), .in11(1'b0), .in12(subtractor_1_bout), .in13(1'b0), .in14(1'b0),
    .in15(1'b0), .out(Signed_Overflow), .sel(AluOP));

  // Other names for the same wires on the sheet: CF = UnSigned_Overflow; OF = Signed_Overflow;
  //   Result2[31:0] = Result_2; S[3:0] = AluOP

  // Notes on the sheet:
  //   ALU
  //   First input
  //   Decimal representations
  //   Second input
  //   Input pins
  //   Output pins
  //   Debug area
endmodule

module EX_MEM (
  input  Clock,
  input  EX_Clear,
  input  EX_Enable,
  input  [31:0] EX_PC,
  input  [31:0] EX_ALURes,
  input  [31:0] EX_ALURes2,
  input  [4:0] EX_rd,
  input  [31:0] RT_EX,
  input  Equal_EX,
  input  EX_RegWrite,
  input  EX_MemToReg,
  input  EX_MemRead,
  input  EX_MemWrite,
  input  EX_Branch,
  output [31:0] MEM_PC,
  output [31:0] MEM_ALURes,
  output [31:0] MEM_ALURes2,
  output [4:0] MEM_rd,
  output [31:0] RT_MEM,
  output Equal_MEM,
  output MEM_RegWrite,
  output MEM_MemToReg,
  output MEM_MemRead,
  output MEM_MemWrite,
  output MEM_Branch
);

  wire [31:0] MEM_ALURes2_t;

  Register #(.width(32), .Select("low")) EX_MEM_PC (.D(EX_PC), .en(EX_Enable), .Q(MEM_PC), .clk(Clock), .clr(EX_Clear));
  Register #(.width(32), .Select("low")) EX_MEM_ALURes (
    .D(EX_ALURes), .en(EX_Enable), .Q(MEM_ALURes), .clk(Clock), .clr(EX_Clear));
  Register #(.width(32), .Select("low")) EX_MEM_ALURes2 (
    .D(EX_ALURes2), .en(EX_Enable), .Q(MEM_ALURes2_t), .clk(Clock), .clr(EX_Clear));
  Register #(.width(5), .Select("low")) EX_MEM_rd (.D(EX_rd), .en(EX_Enable), .Q(MEM_rd), .clk(Clock), .clr(EX_Clear));
  Register #(.width(32), .Select("low")) EX_MEM_RT (.D(RT_EX), .en(EX_Enable), .Q(RT_MEM), .clk(Clock), .clr(EX_Clear));
  Register #(.width(1), .Select("low")) EX_MEM_Equal (.D(Equal_EX), .Q(Equal_MEM));  // open: en, clk, clr
  Register #(.width(1), .Select("low")) EX_MEM_RegWrite (
    .D(EX_RegWrite), .en(EX_Enable), .Q(MEM_RegWrite), .clk(Clock), .clr(EX_Clear));
  Register #(.width(1), .Select("low")) EX_MEM_MemToReg (
    .D(EX_MemToReg), .en(EX_Enable), .Q(MEM_MemToReg), .clk(Clock), .clr(EX_Clear));
  Register #(.width(1), .Select("low")) EX_MEM_MemRead (
    .D(EX_MemRead), .en(EX_Enable), .Q(MEM_MemRead), .clk(Clock), .clr(EX_Clear));
  Register #(.width(1), .Select("low")) EX_MEM_MemWrite (
    .D(EX_MemWrite), .en(EX_Enable), .Q(MEM_MemWrite), .clk(Clock), .clr(EX_Clear));
  Register #(.width(1), .Select("low")) EX_MEM_Branch (
    .D(EX_Branch), .en(EX_Enable), .Q(MEM_Branch), .clk(Clock), .clr(EX_Clear));

  // Other names for the same wires on the sheet: Clear = EX_Clear; Enable = EX_Enable

  // Notes on the sheet:
  //   WB
  //   MEM
  //   Registros de pipeline MIPS: EX/MEM
  //   Datapath
  //   Control
  //   Entradas y salidas
  //   WB
  //   MEM
endmodule

module DataMemory (
  input  [31:0] Address,
  input  [31:0] WriteData,
  input  MemRead,
  input  MemWrite,
  input  Clock,
  output [31:0] ReadData
);

  Demultiplexer #(.select(2), .enable("false")) demultiplexer_1 (
    .in(1'b1), .sel(Address[1:0]));  // open: out0, out1, out2, out3
  RAM #(.addrWidth(10), .bus("separate"), .Select("low")) Byte_0 (
    .addr(Address[11:2]), .din(WriteData[7:0]), .data(ReadData[7:0]), .sel(MemWrite), .clk(Clock),
    .ld(MemRead));  // open: str, clr
  RAM #(.addrWidth(10), .bus("separate"), .Select("low")) Byte_1 (
    .addr(Address[11:2]), .din(WriteData[15:8]), .data(ReadData[15:8]), .sel(MemWrite), .clk(Clock),
    .ld(MemRead));  // open: str, clr
  RAM #(.addrWidth(10), .bus("separate"), .Select("low")) Byte_2 (
    .addr(Address[11:2]), .din(WriteData[23:16]), .data(ReadData[23:16]), .sel(MemWrite), .clk(Clock),
    .ld(MemRead));  // open: str, clr
  RAM #(.addrWidth(10), .bus("separate"), .Select("low")) Byte_3 (
    .addr(Address[11:2]), .din(WriteData[31:24]), .data(ReadData[31:24]), .sel(MemWrite), .clk(Clock),
    .ld(MemRead));  // open: str, clr
endmodule

module MEM_WB (
  input  Clock,
  input  EX_Clear,
  input  EX_Enable,
  input  [31:0] ReadData_MEM,
  input  [31:0] ALUResult_MEM,
  input  [4:0] rd_MEM,
  input  RegWrite_MEM,
  input  MemToReg_MEM,
  output [31:0] ReadData_WB,
  output [31:0] ALUResult_WB,
  output [4:0] rd_WB,
  output RegWrite_WB,
  output MemToReg_WB
);

  Register #(.width(32), .Select("low")) MEM_WB_ReadData (
    .D(ReadData_MEM), .en(EX_Enable), .Q(ReadData_WB), .clk(Clock), .clr(EX_Clear));
  Register #(.width(32), .Select("low")) MEM_WB_ALUResult (
    .D(ALUResult_MEM), .en(EX_Enable), .Q(ALUResult_WB), .clk(Clock), .clr(EX_Clear));
  Register #(.width(5), .Select("low")) MEM_WB_ALUResult_2 (.D(rd_MEM), .Q(rd_WB));  // open: en, clk, clr
  Register #(.width(1), .Select("low")) EX_MEM_MemToReg (
    .D(RegWrite_MEM), .en(EX_Enable), .Q(RegWrite_WB), .clk(Clock), .clr(EX_Clear));
  Register #(.width(1), .Select("low")) EX_MEM_MemToReg_2 (
    .D(MemToReg_MEM), .en(EX_Enable), .Q(MemToReg_WB), .clk(Clock), .clr(EX_Clear));

  // Other names for the same wires on the sheet: ALUReslut_MEM[31:0] = ALUResult_MEM; Clear = EX_Clear;
  //   Enable = EX_Enable

  // Notes on the sheet:
  //   WB
  //   Datapath
  //   Control
  //   WB
endmodule

// Forwarding Unit
module ForwardingUnit (
  input  [4:0] ID_EX_rs,
  input  [4:0] EX_MEM_rd,
  input  EX_MEM_RegWrite,
  input  [4:0] ID_EX_rt,
  input  [4:0] MEM_WB_rd,
  input  MEM_WB_RegWrite,
  output [1:0] ForwardA,
  output [1:0] ForwardB
);

  wire and_3_out, and_4_out, comparator_1_gt, comparator_2_gt, comparator_3_eq, comparator_4_eq,
       comparator_5_eq, comparator_6_eq;

  Comparator #(.width(1)) comparator_1 (.a(EX_MEM_RegWrite), .b(1'b0), .gt(comparator_1_gt));  // open: eq, lt
  Comparator #(.width(5)) comparator_2 (.a(EX_MEM_rd), .b({5{1'b0}}), .gt(comparator_2_gt));  // open: eq, lt
  Comparator #(.width(5)) comparator_3 (.a(EX_MEM_rd), .b(ID_EX_rs), .eq(comparator_3_eq));  // open: gt, lt
  Comparator #(.width(5)) comparator_4 (.a(EX_MEM_rd), .b(ID_EX_rt), .eq(comparator_4_eq));  // open: gt, lt
  Comparator #(.width(5)) comparator_5 (.a(MEM_WB_rd), .b(ID_EX_rs), .eq(comparator_5_eq));  // open: gt, lt
  Comparator #(.width(5)) comparator_6 (.a(MEM_WB_rd), .b(ID_EX_rt), .eq(comparator_6_eq));  // open: gt, lt
  and and_1 (ForwardA[1], comparator_1_gt, comparator_2_gt, comparator_3_eq);
  and and_2 (ForwardB[1], comparator_1_gt, comparator_2_gt, comparator_4_eq);
  and and_3 (and_3_out, comparator_1_gt, comparator_2_gt, comparator_5_eq, ~ForwardA[1]);  // AND_Gate
  and and_4 (and_4_out, comparator_1_gt, comparator_2_gt, comparator_6_eq, ~ForwardB[1]);  // AND_Gate
  assign ForwardA = {{1{1'b0}}, and_3_out};  // Bit_Extender bit_extender_1
  assign ForwardB = {{1{1'b0}}, and_4_out};  // Bit_Extender bit_extender_2
  // also tied to GND on the sheet: {ForwardA[0], ForwardB[0]}

  // Notes on the sheet:
  //   Entradas y Salidas
endmodule

module HazardDetectionUnit (
  input  [4:0] ID_EX_rs,
  input  [4:0] ID_EX_rt,
  input  ID_EX_MemRead,
  input  BranchOrJump,
  input  Clock,
  output IF_Stall,
  output ID_Sttall,
  output IF_Flush
);

  wire comparator_1_eq, d_ff_1_q;

  Comparator #(.width(5)) comparator_1 (.a(ID_EX_rs), .b(ID_EX_rt), .eq(comparator_1_eq));  // open: gt, lt
  and and_1 (ID_Sttall, comparator_1_eq, ID_EX_MemRead);
  and and_2 (IF_Flush, ~Clock, d_ff_1_q);  // AND_Gate
  D_Flip_Flop #(.trigger("falling"), .Pre_Clr_Positions("LEGACY"), .enable("true"), .NewFFLayout("false")) d_ff_1 (
    .clk(Clock), .D(BranchOrJump), .Q(d_ff_1_q));  // open: Qn, preset, en, reset

  assign IF_Stall = ID_Sttall;

  // Other names for the same wires on the sheet: EX_MEM_rd = ID_EX_MemRead; ID_Stall = ID_Sttall

  // Notes on the sheet:
  //   Entradas y Salidas
endmodule
