// Logisim project AluTesterRefinedB82957.circ as structural Verilog: 2 circuits, main circuit main
module main (
  input  [31:0] X,
  input  [31:0] Y,
  input  [3:0] Switch,
  output Signed_Overflow,
  output Equal,
  output [31:0] Result,
  output [31:0] Result_2
);

  wire add_out2, sub_out2, xnor_1_out;
  wire [0:0] slt_out, sltu_out;
  wire [31:0] add_out, addu_out, and_out, divu_out, divu_out2, multu_out, multu_out2, or_out, sll_out,
       sra_out, srl_out, sub_out, subu_out;

  Adder #(.width(32)) adder_1 (.a(X), .b(Y), .out(add_out));  // open: cin, cout
  Adder #(.width(32)) adder_2 (.a(X), .b(Y), .out(addu_out));  // open: cin, cout
  Shifter #(.width(32)) shifter_1 (.in(X), .\dist (Y[4:0]), .out(sll_out));
  Shifter #(.width(32), .shift("lr")) shifter_2 (.in(X), .\dist (Y[4:0]), .out(srl_out));
  xnor xnor_1 (xnor_1_out, X[31], Y[31]);
  and and_1 (add_out2, xnor_1_out, add_out[31]);
  Multiplexer #(.select(4), .width(32)) multiplexer_1 (
    .in0(sll_out), .in1(srl_out), .in2(sra_out), .in3(multu_out), .in4(divu_out), .in5(add_out),
    .in6(addu_out), .in7(sub_out), .in8(subu_out), .in9(and_out), .in10(or_out),
    .in11({{31{1'b0}}, slt_out[0]}), .in12({{31{1'b0}}, sltu_out[0]}), .out(Result), .sel(Switch));  // open: in13, in14, in15, en
  Shifter #(.width(32), .shift("ar")) shifter_3 (.in(X), .\dist (Y[4:0]), .out(sra_out));
  Multiplexer #(.select(4), .width(32)) multiplexer_2 (
    .in0({32{1'b0}}), .in1({32{1'b0}}), .in2({32{1'b0}}), .in3(multu_out2), .in4(divu_out2),
    .in5({32{1'b0}}), .in6({32{1'b0}}), .in7({32{1'b0}}), .in8({32{1'b0}}), .in9({32{1'b0}}),
    .in10({32{1'b0}}), .in11({32{1'b0}}), .in12({32{1'b0}}), .in13({32{1'b0}}), .in14({32{1'b0}}),
    .in15({32{1'b0}}), .out(Result_2), .sel(Switch));  // open: en
  assign and_out = Y & X;  // AND_Gate and_2, 32 bits wide
  Subtractor #(.width(32)) subtractor_1 (.a(X), .b(Y), .out(subu_out));  // open: bin, bout
  Subtractor #(.width(32)) subtractor_2 (.a(X), .b(Y), .out(sub_out), .bout(sub_out2));  // open: bin
  assign or_out = Y | X;  // OR_Gate or_1, 32 bits wide
  Divider #(.width(32)) divider_1 (.a(X), .b(Y), .out(divu_out), .rem(divu_out2));  // open: upper
  Comparator #(.width(32), .mode("unsigned")) comparator_1 (.a(X), .b(Y), .eq(Equal), .lt(sltu_out[0]));  // open: gt
  Comparator #(.width(32)) comparator_2 (.a(X), .b(Y), .lt(slt_out[0]));  // open: gt, eq
  Multiplier #(.width(32)) multiplier_1 (.a(X), .b(Y), .out(multu_out), .cout(multu_out2));  // open: cin
  Multiplexer #(.select(4)) multiplexer_3 (
    .in0(1'b0), .in1(1'b0), .in2(1'b0), .in3(1'b0), .in4(1'b0), .in5(add_out2), .in6(1'b0), .in7(sub_out2),
    .in8(1'b0), .in9(1'b0), .in10(1'b0), .in11(1'b0), .in12(1'b0), .in13(1'b0), .in14(1'b0), .in15(1'b0),
    .out(Signed_Overflow), .sel(Switch));  // open: en

  // Other names for the same wires on the sheet: last_bit = add_out[31]; overflow = Signed_Overflow; S[3:0] = Switch

  // Notes on the sheet:
  //   INPUTS to your circuit
  //   OUTPUTS from your circuit
endmodule

module mainCircuit (
  input  [31:0] Data_1,
  input  [31:0] Data_2,
  input  [3:0] Switcher_to_choose_operation,
  output out,
  output [31:0] out_5,
  output [31:0] out_6
);

  main main_1 (
    .Switch(Switcher_to_choose_operation), .X(Data_1), .Equal(out), .Result(out_5), .Y(Data_2),
    .Result_2(out_6));  // open: Signed_Overflow
endmodule
