// Logisim project MIPCPU.circ as structural Verilog: 5 circuits, main circuit main
module main (
);

  wire Clock;
  wire [3:0] adder_1_out, PC;

  Counter #(.width(4), .max('hf)) counter_1 (
    .D(adder_1_out), .Q(PC), .clk(Clock));  // open: load, count, carry, clr, preset, down
  Adder #(.width(4)) adder_1 (.a(PC), .b(4'b0100), .out(adder_1_out));  // open: cin, cout
  Clock clock_1 (.out(Clock));
  ROM #(.addrWidth(4), .dataWidth(32), .Select("low")) Instruction_Memory (.addr(PC));  // open: data
  _32_bit_ALU u_32_bit_alu_1 ();  // open: A, B, Sub, Op, out_5, Zero_flag
  ControlUnit controlunit_1 ();  // open: Instruction_Selector, Selected_Instruction, MEM, WB, EX, Offset
  _32Bit_Register_File u_32bit_register_file_1 ();  // open: Write_Register, Read_Register_1, Read_Register_2, Write_Data, RegWrite, Clock, Read_Data_1, Read_Data_2
endmodule

module _32Bit_Register_File (
  input  [3:0] Write_Register,
  input  [3:0] Read_Register_1,
  input  [3:0] Read_Register_2,
  input  [31:0] Write_Data,
  input  RegWrite,
  input  Clock,
  output [31:0] Read_Data_1,
  output [31:0] Read_Data_2
);

  wire and_1_out, and_2_out, and_3_out, and_4_out, and_5_out, and_6_out, and_7_out, and_8_out, and_9_out,
       and_10_out, and_11_out, and_12_out, and_13_out, and_14_out, and_15_out, and_16_out, decoder_1_out0,
       decoder_1_out1, decoder_1_out2, decoder_1_out3, decoder_1_out4, decoder_1_out5, decoder_1_out6,
       decoder_1_out7, decoder_1_out8, decoder_1_out9, decoder_1_out10, decoder_1_out11, decoder_1_out12,
       decoder_1_out13, decoder_1_out14, decoder_1_out15;
  wire [31:0] register_1_q, register_2_q, register_3_q, register_4_q, register_5_q, register_6_q,
       register_7_q, register_8_q, register_9_q, register_10_q, register_11_q, register_12_q, register_13_q,
       register_14_q, register_15_q, register_16_q;

  Decoder #(.select(4)) decoder_1 (
    .out0(decoder_1_out0), .out1(decoder_1_out1), .out2(decoder_1_out2), .out3(decoder_1_out3),
    .out4(decoder_1_out4), .out5(decoder_1_out5), .out6(decoder_1_out6), .out7(decoder_1_out7),
    .out8(decoder_1_out8), .out9(decoder_1_out9), .out10(decoder_1_out10), .out11(decoder_1_out11),
    .out12(decoder_1_out12), .out13(decoder_1_out13), .out14(decoder_1_out14), .out15(decoder_1_out15),
    .sel(Write_Register));  // open: en
  and and_1 (and_1_out, decoder_1_out0, RegWrite);
  and and_2 (and_2_out, decoder_1_out1, RegWrite);
  and and_3 (and_3_out, decoder_1_out2, RegWrite);
  and and_4 (and_4_out, decoder_1_out3, RegWrite);
  and and_5 (and_5_out, decoder_1_out4, RegWrite);
  and and_6 (and_6_out, decoder_1_out5, RegWrite);
  and and_7 (and_7_out, decoder_1_out6, RegWrite);
  and and_8 (and_8_out, decoder_1_out7, RegWrite);
  Register #(.width(32), .Select("low")) register_1 (
    .D(Write_Data), .en(and_1_out), .Q(register_1_q), .clk(Clock));  // open: clr
  Register #(.width(32), .Select("low")) register_2 (
    .D(Write_Data), .en(and_2_out), .Q(register_2_q), .clk(Clock));  // open: clr
  Register #(.width(32), .Select("low")) register_3 (
    .D(Write_Data), .en(and_3_out), .Q(register_3_q), .clk(Clock));  // open: clr
  Register #(.width(32), .Select("low")) register_4 (
    .D(Write_Data), .en(and_4_out), .Q(register_4_q), .clk(Clock));  // open: clr
  Register #(.width(32), .Select("low")) register_5 (
    .D(Write_Data), .en(and_5_out), .Q(register_5_q), .clk(Clock));  // open: clr
  Register #(.width(32), .Select("low")) register_6 (
    .D(Write_Data), .en(and_6_out), .Q(register_6_q), .clk(Clock));  // open: clr
  Register #(.width(32), .Select("low")) register_7 (
    .D(Write_Data), .en(and_7_out), .Q(register_7_q), .clk(Clock));  // open: clr
  Register #(.width(32), .Select("low")) register_8 (
    .D(Write_Data), .en(and_8_out), .Q(register_8_q), .clk(Clock));  // open: clr
  and and_9 (and_9_out, decoder_1_out8, RegWrite);
  and and_10 (and_10_out, decoder_1_out9, RegWrite);
  and and_11 (and_11_out, decoder_1_out10, RegWrite);
  and and_12 (and_12_out, decoder_1_out11, RegWrite);
  and and_13 (and_13_out, decoder_1_out12, RegWrite);
  and and_14 (and_14_out, decoder_1_out13, RegWrite);
  and and_15 (and_15_out, decoder_1_out14, RegWrite);
  and and_16 (and_16_out, decoder_1_out15, RegWrite);
  Register #(.width(32), .Select("low")) register_9 (
    .D(Write_Data), .en(and_9_out), .Q(register_9_q), .clk(Clock));  // open: clr
  Register #(.width(32), .Select("low")) register_10 (
    .D(Write_Data), .en(and_10_out), .Q(register_10_q), .clk(Clock));  // open: clr
  Register #(.width(32), .Select("low")) register_11 (
    .D(Write_Data), .en(and_11_out), .Q(register_11_q), .clk(Clock));  // open: clr
  Register #(.width(32), .Select("low")) register_12 (
    .D(Write_Data), .en(and_12_out), .Q(register_12_q), .clk(Clock));  // open: clr
  Register #(.width(32), .Select("low")) register_13 (
    .D(Write_Data), .en(and_13_out), .Q(register_13_q), .clk(Clock));  // open: clr
  Register #(.width(32), .Select("low")) register_14 (
    .D(Write_Data), .en(and_14_out), .Q(register_14_q), .clk(Clock));  // open: clr
  Register #(.width(32), .Select("low")) register_15 (
    .D(Write_Data), .en(and_15_out), .Q(register_15_q), .clk(Clock));  // open: clr
  Register #(.width(32), .Select("low")) register_16 (
    .D(Write_Data), .en(and_16_out), .Q(register_16_q), .clk(Clock));  // open: clr
  Multiplexer #(.select(4), .width(32)) multiplexer_1 (
    .in0(register_1_q), .in1(register_2_q), .in2(register_3_q), .in3(register_4_q), .in4(register_5_q),
    .in5(register_6_q), .in6(register_7_q), .in7(register_8_q), .in8(register_9_q), .in9(register_10_q),
    .in10(register_11_q), .in11(register_12_q), .in12(register_13_q), .in13(register_14_q),
    .in14(register_15_q), .in15(register_16_q), .out(Read_Data_1), .sel(Read_Register_1));  // open: en
  Multiplexer #(.select(4), .width(32)) multiplexer_2 (
    .in0(register_1_q), .in1(register_2_q), .in2(register_3_q), .in3(register_4_q), .in4(register_5_q),
    .in5(register_6_q), .in6(register_7_q), .in7(register_8_q), .in8(register_9_q), .in9(register_10_q),
    .in10(register_11_q), .in11(register_12_q), .in12(register_13_q), .in13(register_14_q),
    .in14(register_15_q), .in15(register_16_q), .out(Read_Data_2), .sel(Read_Register_2));  // open: en
endmodule

module _1_bit_ALU (
  input  Sub,
  input  Cin,
  input  [2:0] in_3,
  input  A,
  input  B,
  input  Less,
  output Result,
  output C_out,
  output out_9
);

  wire and_1_out, nor_1_out, or_1_out, xor_1_out, xor_2_out;

  or or_1 (or_1_out, A, B);
  Adder #(.width(1)) adder_1 (.a(A), .b(xor_1_out), .out(out_9), .cin(Cin), .cout(C_out));
  xor xor_1 (xor_1_out, B, Sub);
  and and_1 (and_1_out, A, B);
  xor xor_2 (xor_2_out, A, B);
  nor nor_1 (nor_1_out, A, B);
  Multiplexer #(.select(3)) multiplexer_1 (
    .in0(and_1_out), .in1(or_1_out), .in2(xor_2_out), .in3(nor_1_out), .in4(out_9), .in5(Less), .out(Result),
    .sel(in_3));  // open: in6, in7, en
endmodule

module _32_bit_ALU (
  input  Sub,
  input  [2:0] Op,
  input  [31:0] A,
  input  [31:0] B,
  output [31:0] out_5,
  output Zero_flag
);

  wire n1_bit_alu_1_c_out, n1_bit_alu_2_c_out, n1_bit_alu_3_c_out, n1_bit_alu_4_c_out, n1_bit_alu_5_c_out,
       n1_bit_alu_6_c_out, n1_bit_alu_7_c_out, n1_bit_alu_8_c_out, n1_bit_alu_9_c_out, n1_bit_alu_10_c_out,
       n1_bit_alu_11_c_out, n1_bit_alu_12_c_out, n1_bit_alu_13_c_out, n1_bit_alu_14_c_out,
       n1_bit_alu_15_c_out, n1_bit_alu_16_c_out, n1_bit_alu_17_c_out, n1_bit_alu_18_c_out,
       n1_bit_alu_19_c_out, n1_bit_alu_20_c_out, n1_bit_alu_21_c_out, n1_bit_alu_22_c_out,
       n1_bit_alu_23_c_out, n1_bit_alu_24_c_out, n1_bit_alu_25_c_out, n1_bit_alu_26_c_out,
       n1_bit_alu_27_c_out, n1_bit_alu_28_c_out, n1_bit_alu_29_c_out, n1_bit_alu_30_c_out,
       n1_bit_alu_31_c_out, n1_bit_alu_32_out_9;

  _1_bit_ALU u_1_bit_alu_1 (
    .in_3(Op), .A(A[0]), .B(B[0]), .Less(n1_bit_alu_32_out_9), .Result(out_5[0]), .Sub(Sub), .Cin(Sub),
    .C_out(n1_bit_alu_1_c_out));  // open: out_9
  _1_bit_ALU u_1_bit_alu_2 (
    .in_3(Op), .A(A[1]), .B(B[1]), .Less(1'b0), .Result(out_5[1]), .Sub(Sub), .Cin(n1_bit_alu_1_c_out),
    .C_out(n1_bit_alu_2_c_out));  // open: out_9
  _1_bit_ALU u_1_bit_alu_3 (
    .in_3(Op), .A(A[2]), .B(B[2]), .Less(1'b0), .Result(out_5[2]), .Sub(Sub), .Cin(n1_bit_alu_2_c_out),
    .C_out(n1_bit_alu_3_c_out));  // open: out_9
  _1_bit_ALU u_1_bit_alu_4 (
    .in_3(Op), .A(A[3]), .B(B[3]), .Less(1'b0), .Result(out_5[3]), .Sub(Sub), .Cin(n1_bit_alu_3_c_out),
    .C_out(n1_bit_alu_4_c_out));  // open: out_9
  _1_bit_ALU u_1_bit_alu_5 (
    .in_3(Op), .A(A[4]), .B(B[4]), .Less(1'b0), .Result(out_5[4]), .Sub(Sub), .Cin(n1_bit_alu_4_c_out),
    .C_out(n1_bit_alu_5_c_out));  // open: out_9
  _1_bit_ALU u_1_bit_alu_6 (
    .in_3(Op), .A(A[5]), .B(B[5]), .Less(1'b0), .Result(out_5[5]), .Sub(Sub), .Cin(n1_bit_alu_5_c_out),
    .C_out(n1_bit_alu_6_c_out));  // open: out_9
  _1_bit_ALU u_1_bit_alu_7 (
    .in_3(Op), .A(A[6]), .B(B[6]), .Less(1'b0), .Result(out_5[6]), .Sub(Sub), .Cin(n1_bit_alu_6_c_out),
    .C_out(n1_bit_alu_7_c_out));  // open: out_9
  _1_bit_ALU u_1_bit_alu_8 (
    .in_3(Op), .A(A[7]), .B(B[7]), .Less(1'b0), .Result(out_5[7]), .Sub(Sub), .Cin(n1_bit_alu_7_c_out),
    .C_out(n1_bit_alu_8_c_out));  // open: out_9
  _1_bit_ALU u_1_bit_alu_9 (
    .in_3(Op), .A(A[8]), .B(B[8]), .Less(1'b0), .Result(out_5[8]), .Sub(Sub), .Cin(n1_bit_alu_8_c_out),
    .C_out(n1_bit_alu_9_c_out));  // open: out_9
  _1_bit_ALU u_1_bit_alu_10 (
    .in_3(Op), .A(A[9]), .B(B[9]), .Less(1'b0), .Result(out_5[9]), .Sub(Sub), .Cin(n1_bit_alu_9_c_out),
    .C_out(n1_bit_alu_10_c_out));  // open: out_9
  _1_bit_ALU u_1_bit_alu_11 (
    .in_3(Op), .A(A[10]), .B(B[10]), .Less(1'b0), .Result(out_5[10]), .Sub(Sub), .Cin(n1_bit_alu_10_c_out),
    .C_out(n1_bit_alu_11_c_out));  // open: out_9
  _1_bit_ALU u_1_bit_alu_12 (
    .in_3(Op), .A(A[11]), .B(B[11]), .Less(1'b0), .Result(out_5[11]), .Sub(Sub), .Cin(n1_bit_alu_11_c_out),
    .C_out(n1_bit_alu_12_c_out));  // open: out_9
  _1_bit_ALU u_1_bit_alu_13 (
    .in_3(Op), .A(A[12]), .B(B[12]), .Less(1'b0), .Result(out_5[12]), .Sub(Sub), .Cin(n1_bit_alu_12_c_out),
    .C_out(n1_bit_alu_13_c_out));  // open: out_9
  _1_bit_ALU u_1_bit_alu_14 (
    .in_3(Op), .A(A[13]), .B(B[13]), .Less(1'b0), .Result(out_5[13]), .Sub(Sub), .Cin(n1_bit_alu_13_c_out),
    .C_out(n1_bit_alu_14_c_out));  // open: out_9
  _1_bit_ALU u_1_bit_alu_15 (
    .in_3(Op), .A(A[14]), .B(B[14]), .Less(1'b0), .Result(out_5[14]), .Sub(Sub), .Cin(n1_bit_alu_14_c_out),
    .C_out(n1_bit_alu_15_c_out));  // open: out_9
  _1_bit_ALU u_1_bit_alu_16 (
    .in_3(Op), .A(A[15]), .B(B[15]), .Less(1'b0), .Result(out_5[15]), .Sub(Sub), .Cin(n1_bit_alu_15_c_out),
    .C_out(n1_bit_alu_16_c_out));  // open: out_9
  _1_bit_ALU u_1_bit_alu_17 (
    .in_3(Op), .A(A[16]), .B(B[16]), .Less(1'b0), .Result(out_5[16]), .Sub(Sub), .Cin(n1_bit_alu_16_c_out),
    .C_out(n1_bit_alu_17_c_out));  // open: out_9
  _1_bit_ALU u_1_bit_alu_18 (
    .in_3(Op), .A(A[17]), .B(B[17]), .Less(1'b0), .Result(out_5[17]), .Sub(Sub), .Cin(n1_bit_alu_17_c_out),
    .C_out(n1_bit_alu_18_c_out));  // open: out_9
  _1_bit_ALU u_1_bit_alu_19 (
    .in_3(Op), .A(A[18]), .B(B[18]), .Less(1'b0), .Result(out_5[18]), .Sub(Sub), .Cin(n1_bit_alu_18_c_out),
    .C_out(n1_bit_alu_19_c_out));  // open: out_9
  _1_bit_ALU u_1_bit_alu_20 (
    .in_3(Op), .A(A[19]), .B(B[19]), .Less(1'b0), .Result(out_5[19]), .Sub(Sub), .Cin(n1_bit_alu_19_c_out),
    .C_out(n1_bit_alu_20_c_out));  // open: out_9
  _1_bit_ALU u_1_bit_alu_21 (
    .in_3(Op), .A(A[20]), .B(B[20]), .Less(1'b0), .Result(out_5[20]), .Sub(Sub), .Cin(n1_bit_alu_20_c_out),
    .C_out(n1_bit_alu_21_c_out));  // open: out_9
  _1_bit_ALU u_1_bit_alu_22 (
    .in_3(Op), .A(A[21]), .B(B[21]), .Less(1'b0), .Result(out_5[21]), .Sub(Sub), .Cin(n1_bit_alu_21_c_out),
    .C_out(n1_bit_alu_22_c_out));  // open: out_9
  _1_bit_ALU u_1_bit_alu_23 (
    .in_3(Op), .A(A[22]), .B(B[22]), .Less(1'b0), .Result(out_5[22]), .Sub(Sub), .Cin(n1_bit_alu_22_c_out),
    .C_out(n1_bit_alu_23_c_out));  // open: out_9
  _1_bit_ALU u_1_bit_alu_24 (
    .in_3(Op), .A(A[23]), .B(B[23]), .Less(1'b0), .Result(out_5[23]), .Sub(Sub), .Cin(n1_bit_alu_23_c_out),
    .C_out(n1_bit_alu_24_c_out));  // open: out_9
  _1_bit_ALU u_1_bit_alu_25 (
    .in_3(Op), .A(A[24]), .B(B[24]), .Less(1'b0), .Result(out_5[24]), .Sub(Sub), .Cin(n1_bit_alu_24_c_out),
    .C_out(n1_bit_alu_25_c_out));  // open: out_9
  _1_bit_ALU u_1_bit_alu_26 (
    .in_3(Op), .A(A[25]), .B(B[25]), .Less(1'b0), .Result(out_5[25]), .Sub(Sub), .Cin(n1_bit_alu_25_c_out),
    .C_out(n1_bit_alu_26_c_out));  // open: out_9
  _1_bit_ALU u_1_bit_alu_27 (
    .in_3(Op), .A(A[26]), .B(B[26]), .Less(1'b0), .Result(out_5[26]), .Sub(Sub), .Cin(n1_bit_alu_26_c_out),
    .C_out(n1_bit_alu_27_c_out));  // open: out_9
  _1_bit_ALU u_1_bit_alu_28 (
    .in_3(Op), .A(A[27]), .B(B[27]), .Less(1'b0), .Result(out_5[27]), .Sub(Sub), .Cin(n1_bit_alu_27_c_out),
    .C_out(n1_bit_alu_28_c_out));  // open: out_9
  _1_bit_ALU u_1_bit_alu_29 (
    .in_3(Op), .A(A[28]), .B(B[28]), .Less(1'b0), .Result(out_5[28]), .Sub(Sub), .Cin(n1_bit_alu_28_c_out),
    .C_out(n1_bit_alu_29_c_out));  // open: out_9
  _1_bit_ALU u_1_bit_alu_30 (
    .in_3(Op), .A(A[29]), .B(B[29]), .Less(1'b0), .Result(out_5[29]), .Sub(Sub), .Cin(n1_bit_alu_29_c_out),
    .C_out(n1_bit_alu_30_c_out));  // open: out_9
  _1_bit_ALU u_1_bit_alu_31 (
    .in_3(Op), .A(A[30]), .B(B[30]), .Less(1'b0), .Result(out_5[30]), .Sub(Sub), .Cin(n1_bit_alu_30_c_out),
    .C_out(n1_bit_alu_31_c_out));  // open: out_9
  _1_bit_ALU u_1_bit_alu_32 (
    .in_3(Op), .A(A[31]), .B(B[31]), .Less(1'b0), .Result(out_5[31]), .Sub(Sub), .Cin(n1_bit_alu_31_c_out),
    .out_9(n1_bit_alu_32_out_9));  // open: C_out
  nor nor_1 (Zero_flag, out_5[0], out_5[1], out_5[2], out_5[3], out_5[4], out_5[5], out_5[6], out_5[7], out_5[8], out_5[9], out_5[10], out_5[11], out_5[12], out_5[13], out_5[14], out_5[15], out_5[16], out_5[17], out_5[18], out_5[19], out_5[20], out_5[21], out_5[22], out_5[23], out_5[24], out_5[25], out_5[26], out_5[27], out_5[28], out_5[29], out_5[30], out_5[31]);
endmodule

module ControlUnit (
  input  [1:0] WB,
  input  [2:0] MEM,
  input  [3:0] EX,
  input  [9:0] Instruction_Selector,
  input  [22:0] Offset,
  output [31:0] Selected_Instruction
);

  ROM #(.addrWidth(10), .dataWidth(32), .Select("low")) Instruction_Memory (
    .addr(Instruction_Selector), .data({Offset, EX, MEM, WB}));

  assign Selected_Instruction = {Offset, EX, MEM, WB};

  // Notes on the sheet:
  //   contents of Instruction_Memory (hex, n*v repeats v):
  //   0 1 10 11 100 101
endmodule
