// Logisim project CPU.circ as structural Verilog: 8 circuits, main circuit main
module main (
);

  wire Clock, controlunit_1_p5, controlunit_1_p6, controlunit_1_p7, controlunit_1_p9, controlunit_1_p10,
       controlunit_1_p11, controlunit_1_p12, controlunit_1_p13, RegDst, RegWrite;
  wire [1:0] PC_SELECTOR;
  wire [3:0] controlunit_1_p4;
  wire [4:0] multiplexer_2_out, WriteReg;
  wire [31:0] bit_extender_1_out, bit_extender_2_out, ID_PC_4, if_id_1_id_inst, Instruction_Memory_data,
       n32bit_registerfile_1_drs, n32bit_registerfile_1_drt, PC_4, PC_BRANCH, PC_J, PC_JAL,
       Program_Counter_q, WriteData;

  Clock clock_1 (.out(Clock));
  Register #(.width(32), .Select("low")) Program_Counter (
    .D(PC_4), .Q(Program_Counter_q), .clk(Clock));  // open: en, clr
  Multiplexer #(.select(2), .width(32), .enable("false")) multiplexer_1 (
    .in0(PC_4), .in1(PC_BRANCH), .in2(PC_J), .in3(PC_JAL), .sel(PC_SELECTOR));  // open: out
  Adder #(.width(32)) adder_1 (.a(Program_Counter_q), .b(32'h4), .out(PC_4));  // open: cin, cout
  ROM #(.addrWidth(9), .dataWidth(32), .Select("low")) Instruction_Memory (
    .addr(Program_Counter_q[8:0]), .data(Instruction_Memory_data));
  // Probe on PC_4
  IF_ID if_id_1 (
    .IF_Inst(Instruction_Memory_data), .IF_PC_4(PC_4), .CLK(Clock), .ID_Inst(if_id_1_id_inst),
    .ID_PC_4(ID_PC_4));  // open: En, Clear
  // Probe on ID_PC_4
  // ControlUnit controlunit_1: pin names not known; wires that end beside it: if_id_1_id_inst[5:0], if_id_1_id_inst[31:26], Clock, controlunit_1_p4, controlunit_1_p5, controlunit_1_p6, controlunit_1_p7, RegDst, controlunit_1_p9, controlunit_1_p10, controlunit_1_p11, controlunit_1_p12, controlunit_1_p13
  _32Bit_RegisterFile u_32bit_registerfile_1 (
    .clock(Clock), .rs(if_id_1_id_inst[25:21]), .rt(if_id_1_id_inst[20:16]), .rd(WriteReg),
    .RegWrite(RegWrite), .drs(n32bit_registerfile_1_drs), .drt(n32bit_registerfile_1_drt),
    .WriteData(WriteData));
  assign bit_extender_1_out = {{16{if_id_1_id_inst[15]}}, if_id_1_id_inst[15:0]};  // Bit_Extender bit_extender_1
  assign bit_extender_2_out = {{27{1'b0}}, if_id_1_id_inst[10:6]};  // Bit_Extender bit_extender_2
  Multiplexer #(.width(5), .enable("false")) multiplexer_2 (
    .in0(if_id_1_id_inst[20:16]), .in1(if_id_1_id_inst[15:11]), .out(multiplexer_2_out), .sel(RegDst));
  ID_EX id_ex_1 (
    .PC___4(ID_PC_4), .Imm(bit_extender_1_out), .Shamt(bit_extender_2_out), .CRS(n32bit_registerfile_1_drs),
    .CRT(n32bit_registerfile_1_drt), .WriteReg(multiplexer_2_out), .RegWrite_ID(controlunit_1_p5),
    .MemToReg_ID(controlunit_1_p6), .IsBranch_ID(controlunit_1_p10), .MemRead_ID(controlunit_1_p11),
    .MemWrite_ID(controlunit_1_p12), .ALUSrc_ID(controlunit_1_p13), .ALUOp_ID(controlunit_1_p4));  // open: Clock, Clear, Enable, out_17, out_20, out_21, out_18, out_19, out_22, ALUOp_EX, RegWrite_EX, MemToReg_EX, IsBranch_EX, MemRead_EX, MemWrite_EX, ALUSrc_EX

  // Notes on the sheet:
  //   Estudiantes: Marco Ferraro, Gabriel Revillat
  //   Proyecto Arquitectura de Computadores
  //   Updated PC
endmodule

// Reg File
module _32Bit_RegisterFile (
  input  clock,
  input  [4:0] rs,
  input  [4:0] rt,
  input  [4:0] rd,
  input  RegWrite,
  input  [31:0] WriteData,
  output [31:0] drs,
  output [31:0] drt
);

  wire demultiplexer_1_out0, demultiplexer_1_out1, demultiplexer_1_out2, demultiplexer_1_out3,
       demultiplexer_1_out4, demultiplexer_1_out5, demultiplexer_1_out6, demultiplexer_1_out7,
       demultiplexer_1_out8, demultiplexer_1_out9, demultiplexer_1_out10, demultiplexer_1_out11,
       demultiplexer_1_out12, demultiplexer_1_out13, demultiplexer_1_out14, demultiplexer_1_out15,
       demultiplexer_1_out16, demultiplexer_1_out17, demultiplexer_1_out18, demultiplexer_1_out19,
       demultiplexer_1_out20, demultiplexer_1_out21, demultiplexer_1_out22, demultiplexer_1_out23,
       demultiplexer_1_out24, demultiplexer_1_out25, demultiplexer_1_out26, demultiplexer_1_out27,
       demultiplexer_1_out28, demultiplexer_1_out29, demultiplexer_1_out30, demultiplexer_1_out31;
  wire [31:0] register_1_q, register_2_q, register_3_q, register_4_q, register_5_q, register_6_q,
       register_7_q, register_8_q, register_9_q, register_10_q, register_11_q, register_12_q, register_13_q,
       register_14_q, register_15_q, register_16_q, register_17_q, register_18_q, register_20_q,
       register_21_q, register_22_q, register_23_q, register_24_q, register_25_q, register_26_q,
       register_27_q, register_28_q, register_29_q, register_30_q, register_31_q, register_32_q;

  Demultiplexer #(.select(5), .enable("false")) demultiplexer_1 (
    .out0(demultiplexer_1_out0), .out1(demultiplexer_1_out1), .out2(demultiplexer_1_out2),
    .out3(demultiplexer_1_out3), .out4(demultiplexer_1_out4), .out5(demultiplexer_1_out5),
    .out6(demultiplexer_1_out6), .out7(demultiplexer_1_out7), .out8(demultiplexer_1_out8),
    .out9(demultiplexer_1_out9), .out10(demultiplexer_1_out10), .out11(demultiplexer_1_out11),
    .out12(demultiplexer_1_out12), .out13(demultiplexer_1_out13), .out14(demultiplexer_1_out14),
    .out15(demultiplexer_1_out15), .out16(demultiplexer_1_out16), .out17(demultiplexer_1_out17),
    .out18(demultiplexer_1_out18), .out19(demultiplexer_1_out19), .out20(demultiplexer_1_out20),
    .out21(demultiplexer_1_out21), .out22(demultiplexer_1_out22), .out23(demultiplexer_1_out23),
    .out24(demultiplexer_1_out24), .out25(demultiplexer_1_out25), .out26(demultiplexer_1_out26),
    .out27(demultiplexer_1_out27), .out28(demultiplexer_1_out28), .out29(demultiplexer_1_out29),
    .out30(demultiplexer_1_out30), .out31(demultiplexer_1_out31), .in(RegWrite), .sel(rd));
  Register #(.width(32), .Select("low")) register_1 (.D(WriteData), .en(1'b0), .Q(register_1_q));  // open: clk, clr
  Register #(.width(32), .Select("low")) register_2 (
    .D(WriteData), .en(demultiplexer_1_out8), .Q(register_2_q), .clk(clock), .clr(clock));
  Register #(.width(32), .Select("low")) register_3 (
    .D(WriteData), .en(demultiplexer_1_out16), .Q(register_3_q), .clk(clock));  // open: clr
  Register #(.width(32), .Select("low")) register_4 (
    .D(WriteData), .en(demultiplexer_1_out24), .Q(register_4_q));  // open: clk, clr
  Register #(.width(32), .Select("low")) register_5 (
    .D(WriteData), .en(demultiplexer_1_out1), .Q(register_5_q), .clk(clock));  // open: clr
  Register #(.width(32), .Select("low")) register_6 (
    .D(WriteData), .en(demultiplexer_1_out9), .Q(register_6_q), .clk(clock));  // open: clr
  Register #(.width(32), .Select("low")) register_7 (
    .D(WriteData), .en(demultiplexer_1_out17), .Q(register_7_q), .clk(clock));  // open: clr
  Register #(.width(32), .Select("low")) register_8 (
    .D(WriteData), .en(demultiplexer_1_out25), .Q(register_8_q), .clk(clock));  // open: clr
  Register #(.width(32), .Select("low")) register_9 (
    .D(WriteData), .en(demultiplexer_1_out2), .Q(register_9_q), .clk(clock));  // open: clr
  Register #(.width(32), .Select("low")) register_10 (
    .D(WriteData), .en(demultiplexer_1_out10), .Q(register_10_q), .clk(clock));  // open: clr
  Register #(.width(32), .Select("low")) register_11 (
    .D(WriteData), .en(demultiplexer_1_out18), .Q(register_11_q), .clk(clock));  // open: clr
  Register #(.width(32), .Select("low")) register_12 (
    .D(WriteData), .en(demultiplexer_1_out26), .Q(register_12_q));  // open: clk, clr
  Register #(.width(32), .Select("low")) register_13 (
    .D(WriteData), .en(demultiplexer_1_out3), .Q(register_13_q), .clk(clock));  // open: clr
  Register #(.width(32), .Select("low")) register_14 (
    .D(WriteData), .en(demultiplexer_1_out11), .Q(register_14_q), .clk(clock));  // open: clr
  Register #(.width(32), .Select("low")) register_15 (
    .D(WriteData), .en(demultiplexer_1_out19), .Q(register_15_q), .clk(clock));  // open: clr
  Register #(.width(32), .Select("low")) register_16 (
    .D(WriteData), .en(demultiplexer_1_out27), .Q(register_16_q));  // open: clk, clr
  Register #(.width(32), .Select("low")) register_17 (
    .D(WriteData), .en(demultiplexer_1_out4), .Q(register_17_q), .clk(clock));  // open: clr
  Register #(.width(32), .Select("low")) register_18 (
    .D(WriteData), .en(demultiplexer_1_out12), .Q(register_18_q), .clk(clock));  // open: clr
  Register #(.width(32), .Select("low")) register_19 (
    .D(WriteData), .en(demultiplexer_1_out20), .Q(register_15_q), .clk(clock));  // open: clr
  Register #(.width(32), .Select("low")) register_20 (
    .D(WriteData), .en(demultiplexer_1_out28), .Q(register_20_q));  // open: clk, clr
  Register #(.width(32), .Select("low")) register_21 (
    .D(WriteData), .en(demultiplexer_1_out5), .Q(register_21_q), .clk(clock));  // open: clr
  Register #(.width(32), .Select("low")) register_22 (
    .D(WriteData), .en(demultiplexer_1_out13), .Q(register_22_q), .clk(clock));  // open: clr
  Register #(.width(32), .Select("low")) register_23 (
    .D(WriteData), .en(demultiplexer_1_out21), .Q(register_23_q), .clk(clock));  // open: clr
  Register #(.width(32), .Select("low")) register_24 (
    .D(WriteData), .en(demultiplexer_1_out29), .Q(register_24_q));  // open: clk, clr
  Register #(.width(32), .Select("low")) register_25 (
    .D(WriteData), .en(demultiplexer_1_out6), .Q(register_25_q), .clk(clock));  // open: clr
  Register #(.width(32), .Select("low")) register_26 (
    .D(WriteData), .en(demultiplexer_1_out14), .Q(register_26_q), .clk(clock));  // open: clr
  Register #(.width(32), .Select("low")) register_27 (
    .D(WriteData), .en(demultiplexer_1_out22), .Q(register_27_q), .clk(clock));  // open: clr
  Register #(.width(32), .Select("low")) register_28 (
    .D(WriteData), .en(demultiplexer_1_out30), .Q(register_28_q));  // open: clk, clr
  Register #(.width(32), .Select("low")) register_29 (
    .D(WriteData), .en(demultiplexer_1_out7), .Q(register_29_q), .clk(clock));  // open: clr
  Register #(.width(32), .Select("low")) register_30 (
    .D(WriteData), .en(demultiplexer_1_out15), .Q(register_30_q), .clk(clock));  // open: clr
  Register #(.width(32), .Select("low")) register_31 (
    .D(WriteData), .en(demultiplexer_1_out23), .Q(register_31_q), .clk(clock));  // open: clr
  Register #(.width(32), .Select("low")) register_32 (
    .D(WriteData), .en(demultiplexer_1_out31), .Q(register_32_q));  // open: clk, clr
  Multiplexer #(.select(5), .width(32), .enable("false")) multiplexer_1 (
    .in0(register_1_q), .in1(register_5_q), .in2(register_9_q), .in3(register_13_q), .in4(register_17_q),
    .in5(register_21_q), .in6(register_25_q), .in7(register_29_q), .in8(register_2_q), .in9(register_6_q),
    .in10(register_10_q), .in11(register_14_q), .in12(register_18_q), .in13(register_22_q),
    .in14(register_26_q), .in15(register_30_q), .in16(register_3_q), .in17(register_7_q),
    .in18(register_11_q), .in19(register_15_q), .in20(register_15_q), .in21(register_23_q),
    .in22(register_27_q), .in23(register_31_q), .in24(register_4_q), .in25(register_8_q),
    .in26(register_12_q), .in27(register_16_q), .in28(register_20_q), .in29(register_24_q),
    .in30(register_28_q), .in31(register_32_q), .out(drs), .sel(rs));
  Multiplexer #(.select(5), .width(32), .enable("false")) multiplexer_2 (
    .in0(register_1_q), .in1(register_5_q), .in2(register_9_q), .in3(register_13_q), .in4(register_17_q),
    .in5(register_21_q), .in6(register_25_q), .in7(register_29_q), .in8(register_2_q), .in9(register_6_q),
    .in10(register_10_q), .in11(register_14_q), .in12(register_18_q), .in13(register_22_q),
    .in14(register_26_q), .in15(register_30_q), .in16(register_3_q), .in17(register_7_q),
    .in18(register_11_q), .in19(register_15_q), .in20(register_15_q), .in21(register_23_q),
    .in22(register_27_q), .in23(register_31_q), .in24(register_4_q), .in25(register_8_q),
    .in26(register_12_q), .in27(register_16_q), .in28(register_20_q), .in29(register_24_q),
    .in30(register_28_q), .in31(register_32_q), .out(drt), .sel(rt));

  // Notes on the sheet:
  //   Register File
endmodule

module IF_ID (
  input  En,
  input  [31:0] IF_Inst,
  input  [31:0] IF_PC_4,
  input  CLK,
  input  Clear,
  output [31:0] ID_Inst,
  output [31:0] ID_PC_4
);

  Register #(.width(32), .Select("low")) Inst (.D(IF_Inst), .en(En), .Q(ID_Inst), .clk(CLK), .clr(Clear));
  Register #(.width(32), .Select("low")) PC (.D(IF_PC_4), .en(En), .Q(ID_PC_4), .clk(CLK), .clr(Clear));
endmodule

// Control Unit
module ControlUnit (
  input  Clock,
  input  EX_Clear,
  input  EX_Enable,
  input  [5:0] OpCode,
  input  [5:0] Function,
  input  [4:0] rt,
  output RegWrite,
  output MemToReg,
  output MemRead,
  output MemWrite,
  output IsBranch,
  output ALUSrc,
  output RegDst,
  output IsJR,
  output IsJump,
  output IsSysCall,
  output [3:0] ALUOp
);

  wire and_4_out, and_5_out, and_7_out, and_8_out, JALR_out, Special_2_out, Special_out, SysCall_out;

  and JR (IsJR, ~Function[5], ~Function[4], Function[3], ~Function[2], ~Function[1], ~Function[0]);  // AND_Gate
  and Special (Special_out, ~OpCode[0], ~OpCode[1], ~OpCode[2], ~OpCode[3], ~OpCode[4], ~OpCode[5]);  // AND_Gate
  and JALR (JALR_out, ~Function[0], ~Function[1], Function[2], ~Function[3], ~Function[4], Function[5]);  // AND_Gate
  and Special_2 (Special_2_out, ~OpCode[0], ~OpCode[1], ~OpCode[2], ~OpCode[3], ~OpCode[4], ~OpCode[5]);  // AND_Gate
  and SysCall (SysCall_out, ~Function[0], ~Function[1], Function[2], Function[3], ~Function[4], ~Function[5]);  // AND_Gate
  RegWriteDecode RegWriteDecoder (.OpCode(OpCode), .RegWrite(RegWrite));
  and and_1 (MemToReg, OpCode[5], ~OpCode[4], ~OpCode[3], ~OpCode[2], OpCode[1], OpCode[0]);  // AND_Gate
  and and_2 (MemRead, OpCode[5], ~OpCode[4], ~OpCode[3], ~OpCode[2], OpCode[1], OpCode[0]);  // AND_Gate
  and and_3 (MemWrite, OpCode[5], ~OpCode[4], OpCode[3], ~OpCode[2], OpCode[1], OpCode[0]);  // AND_Gate
  and and_4 (and_4_out, ~OpCode[5], ~OpCode[4], ~OpCode[3], OpCode[2], ~OpCode[1], OpCode[0]);  // AND_Gate
  and and_5 (and_5_out, ~OpCode[5], ~OpCode[4], ~OpCode[3], OpCode[2], ~OpCode[1], ~OpCode[0]);  // AND_Gate
  ALUSrcDecode ALUSrcDecoder (.OpCode(OpCode), .ALUSrc(ALUSrc));
  and and_6 (RegDst, ~OpCode[5], ~OpCode[4], ~OpCode[3], ~OpCode[2], ~OpCode[1], ~OpCode[0]);  // AND_Gate
  or or_1 (IsBranch, and_4_out, and_5_out);
  and and_7 (and_7_out, IsJR, Special_out);
  and and_8 (and_8_out, Special_out, JALR_out);
  and and_9 (IsSysCall, Special_2_out, SysCall_out);
  or or_2 (IsJump, and_7_out, and_8_out);

  // Other names for the same wires on the sheet: Clear = EX_Clear; Enable = EX_Enable

  // Notes on the sheet:
  //   Control
  //   Entradas y salidas
  //   WB
  //   MEM
  //   EX
endmodule

module ID_EX (
  input  Clock,
  input  Clear,
  input  Enable,
  input  [31:0] PC___4,
  input  [31:0] CRS,
  input  [31:0] CRT,
  input  [31:0] Imm,
  input  [31:0] Shamt,
  input  [4:0] WriteReg,
  input  RegWrite_ID,
  input  MemToReg_ID,
  input  IsBranch_ID,
  input  MemRead_ID,
  input  MemWrite_ID,
  input  ALUSrc_ID,
  input  [3:0] ALUOp_ID,
  output [31:0] out_17,
  output [31:0] out_18,
  output [31:0] out_19,
  output [31:0] out_20,
  output [31:0] out_21,
  output [4:0] out_22,
  output RegWrite_EX,
  output MemToReg_EX,
  output IsBranch_EX,
  output MemRead_EX,
  output MemWrite_EX,
  output ALUSrc_EX,
  output [3:0] ALUOp_EX
);

  Register #(.width(32), .Select("low")) register_1 (.D(PC___4), .en(Enable), .Q(out_17), .clk(Clock), .clr(Enable));
  Register #(.width(32), .Select("low")) register_2 (.D(CRS), .en(Enable), .Q(out_18), .clk(Clock), .clr(Enable));
  Register #(.width(32), .Select("low")) register_3 (.D(CRT), .en(Enable), .Q(out_19), .clk(Clock), .clr(Enable));
  Register #(.width(32), .Select("low")) register_4 (.D(Imm), .en(Enable), .Q(out_20), .clk(Clock), .clr(Enable));
  Register #(.width(32), .Select("low")) register_5 (.D(Shamt), .en(Enable), .Q(out_21), .clk(Clock), .clr(Enable));
  Register #(.width(5), .Select("low")) register_6 (.D(WriteReg), .en(Enable), .Q(out_22), .clk(Clock), .clr(Enable));
  Register #(.width(1), .Select("low")) register_7 (
    .D(RegWrite_ID), .en(Enable), .Q(RegWrite_EX), .clk(Clock), .clr(Enable));
  Register #(.width(1), .Select("low")) register_8 (
    .D(MemToReg_ID), .en(Enable), .Q(MemToReg_EX), .clk(Clock), .clr(Enable));
  Register #(.width(1), .Select("low")) register_9 (
    .D(IsBranch_ID), .en(Enable), .Q(IsBranch_EX), .clk(Clock), .clr(Enable));
  Register #(.width(1), .Select("low")) register_10 (
    .D(MemRead_ID), .en(Enable), .Q(MemRead_EX), .clk(Clock), .clr(Enable));
  Register #(.width(1), .Select("low")) register_11 (
    .D(MemWrite_ID), .en(Enable), .Q(MemWrite_EX), .clk(Clock), .clr(Enable));
  Register #(.width(1), .Select("low")) register_12 (
    .D(ALUSrc_ID), .en(Enable), .Q(ALUSrc_EX), .clk(Clock), .clr(Enable));
  Register #(.width(4), .Select("low")) register_13 (
    .D(ALUOp_ID), .en(Enable), .Q(ALUOp_EX), .clk(Clock), .clr(Enable));

  // Other names for the same wires on the sheet: CRS_EX[31:0] = out_18; CRS_ID[31:0] = CRS; CRT_EX[31:0] = out_19;
  //   CRT_ID[31:0] = CRT; Imm_EX[31:0] = out_20; Imm_ID[31:0] = Imm; PC_4_EX[31:0] = out_17; PC_4_ID[31:0] = PC___4;
  //   Shamt_EX[31:0] = out_21; Shamt_ID[31:0] = Shamt; WriteReg_EX[4:0] = out_22; WriteReg_ID[4:0] = WriteReg

  // Notes on the sheet:
  //   Datapath
  //   Control
  //   WB
  //   MEM
  //   EX
endmodule

module RegWriteDecode (
  input  [5:0] OpCode,
  output RegWrite
);

  wire and_1_out, and_2_out, and_3_out, and_4_out, and_5_out, and_6_out, and_7_out, and_8_out, and_9_out,
       and_10_out;

  and and_1 (and_1_out, ~OpCode[5], ~OpCode[4], ~OpCode[3], ~OpCode[2], ~OpCode[1], ~OpCode[0]);  // AND_Gate
  and and_2 (and_2_out, ~OpCode[5], ~OpCode[4], OpCode[3], ~OpCode[2], ~OpCode[1], ~OpCode[0]);  // AND_Gate
  and and_3 (and_3_out, OpCode[5], ~OpCode[4], ~OpCode[3], ~OpCode[2], OpCode[1], OpCode[0]);  // AND_Gate
  and and_4 (and_4_out, ~OpCode[5], ~OpCode[4], OpCode[3], OpCode[2], ~OpCode[1], ~OpCode[0]);  // AND_Gate
  and and_5 (and_5_out, ~OpCode[5], ~OpCode[4], OpCode[3], OpCode[2], ~OpCode[1], OpCode[0]);  // AND_Gate
  and and_6 (and_6_out, ~OpCode[5], ~OpCode[4], OpCode[3], ~OpCode[2], OpCode[1], ~OpCode[0]);  // AND_Gate
  and and_7 (and_7_out, ~OpCode[5], ~OpCode[4], OpCode[3], ~OpCode[2], ~OpCode[1], OpCode[0]);  // AND_Gate
  and and_8 (and_8_out, ~OpCode[5], ~OpCode[4], OpCode[3], ~OpCode[2], ~OpCode[1], ~OpCode[0]);  // AND_Gate
  and and_9 (and_9_out, ~OpCode[5], ~OpCode[4], ~OpCode[3], ~OpCode[2], OpCode[1], OpCode[0]);  // AND_Gate
  and and_10 (and_10_out, ~OpCode[5], OpCode[4], ~OpCode[3], ~OpCode[2], ~OpCode[1], ~OpCode[0]);  // AND_Gate
  or or_1 (RegWrite, and_1_out, and_2_out, and_3_out, and_4_out, and_5_out, and_6_out, and_7_out, and_8_out, and_9_out, and_10_out);
endmodule

module ALUSrcDecode (
  input  [5:0] OpCode,
  output ALUSrc
);

  wire and_1_out, and_2_out, and_3_out, and_4_out, and_5_out, and_6_out, and_7_out, and_8_out;

  and and_1 (and_1_out, ~OpCode[5], ~OpCode[4], ~OpCode[3], ~OpCode[2], ~OpCode[1], ~OpCode[0]);  // AND_Gate
  and and_2 (and_2_out, OpCode[5], ~OpCode[4], ~OpCode[3], ~OpCode[2], OpCode[1], OpCode[0]);  // AND_Gate
  and and_3 (and_3_out, OpCode[5], ~OpCode[4], OpCode[3], ~OpCode[2], OpCode[1], OpCode[0]);  // AND_Gate
  and and_4 (and_4_out, ~OpCode[5], ~OpCode[4], OpCode[3], OpCode[2], ~OpCode[1], ~OpCode[0]);  // AND_Gate
  and and_5 (and_5_out, ~OpCode[5], ~OpCode[4], OpCode[3], OpCode[2], ~OpCode[1], OpCode[0]);  // AND_Gate
  and and_6 (and_6_out, ~OpCode[5], ~OpCode[4], OpCode[3], ~OpCode[2], OpCode[1], ~OpCode[0]);  // AND_Gate
  and and_7 (and_7_out, ~OpCode[5], ~OpCode[4], OpCode[3], ~OpCode[2], ~OpCode[1], OpCode[0]);  // AND_Gate
  and and_8 (and_8_out, ~OpCode[5], ~OpCode[4], OpCode[3], ~OpCode[2], ~OpCode[1], ~OpCode[0]);  // AND_Gate
  or or_1 (ALUSrc, and_1_out, and_2_out, and_3_out, and_4_out, and_5_out, and_6_out, and_7_out, and_8_out);
endmodule

module FunctionDecode (
  input  [5:0] Function,
  output _0,
  output _1,
  output _2,
  output _3
);

  wire and_1_out, and_2_out, and_3_out, and_4_out, and_5_out, and_6_out, and_7_out, and_8_out, and_9_out,
       and_10_out, and_11_out, and_12_out, and_13_out;

  and and_1 (and_1_out, Function[5], ~Function[4], ~Function[3], Function[2], ~Function[1], Function[0]);  // AND_Gate
  and and_2 (and_2_out, Function[5], ~Function[4], ~Function[3], Function[2], Function[1], Function[0]);  // AND_Gate
  and and_3 (and_3_out, Function[5], ~Function[4], Function[3], ~Function[2], Function[1], ~Function[0]);  // AND_Gate
  and and_4 (and_4_out, Function[5], ~Function[4], Function[3], ~Function[2], Function[1], Function[0]);  // AND_Gate
  or or_1 (_0, and_1_out, and_2_out, and_3_out, and_4_out);
  and and_5 (and_5_out, Function[5], ~Function[4], ~Function[3], ~Function[2], ~Function[1]);  // AND_Gate
  and and_6 (and_6_out, Function[5], ~Function[4], ~Function[3], ~Function[2], ~Function[0]);  // AND_Gate
  and and_7 (and_7_out, Function[5], ~Function[4], ~Function[3], ~Function[1], ~Function[0]);  // AND_Gate
  and and_8 (and_8_out, Function[5], ~Function[4], Function[3], ~Function[2], Function[1], Function[0]);  // AND_Gate
  or or_2 (_1, and_5_out, and_6_out, and_7_out, and_8_out);
  and and_9 (and_9_out, Function[5], ~Function[4], ~Function[3], ~Function[2], Function[1], ~Function[0]);  // AND_Gate
  and and_10 (and_10_out, Function[5], ~Function[4], ~Function[3], Function[2], ~Function[1], ~Function[0]);  // AND_Gate
  and and_11 (and_11_out, ~Function[5], ~Function[4], ~Function[3], ~Function[2], Function[1], ~Function[0]);  // AND_Gate
  and and_12 (and_12_out, Function[5], ~Function[4], ~Function[3], Function[2], Function[1], Function[0]);  // AND_Gate
  and and_13 (and_13_out, Function[5], ~Function[4], Function[3], ~Function[2], Function[1], ~Function[0]);  // AND_Gate
  or or_3 (_2, and_9_out, and_10_out, and_11_out, and_12_out, and_13_out);
endmodule
