// Logisim project ControlUnit.circ as structural Verilog: 1 circuit, main circuit main
module main (
  input  [9:0] in_1,
  output [1:0] WriteBack,
  output [2:0] MEM,
  output [3:0] EX,
  output [22:0] Offset,
  output IsJump,
  output IsSysCall
);

  wire and_1_out, and_2_out, JALR_out, JR_out, Special_2_out, Special_out, SysCall_out;

  ROM #(.addrWidth(10), .dataWidth(32), .Select("low")) rom_1 (.addr(in_1), .data({Offset, EX, MEM, WriteBack}));
  and JR (JR_out, ~WriteBack[0], ~WriteBack[1], ~MEM[0], MEM[1], ~MEM[2], ~EX[0]);  // AND_Gate
  and Special (Special_out, ~Offset[17], ~Offset[18], ~Offset[19], ~Offset[20], ~Offset[21], ~Offset[22]);  // AND_Gate
  and JALR (JALR_out, WriteBack[0], ~WriteBack[1], ~MEM[0], MEM[1], ~MEM[2], ~EX[0]);  // AND_Gate
  and Special_2 (Special_2_out, ~Offset[17], ~Offset[18], ~Offset[19], ~Offset[20], ~Offset[21], ~Offset[22]);  // AND_Gate
  and SysCall (SysCall_out, ~WriteBack[0], ~WriteBack[1], MEM[0], MEM[1], ~MEM[2], ~EX[0]);  // AND_Gate
  and and_1 (and_1_out, JR_out, Special_out);
  and and_2 (and_2_out, Special_out, JALR_out);
  and and_3 (IsSysCall, Special_2_out, SysCall_out);
  or or_1 (IsJump, and_1_out, and_2_out);

  // Other names for the same wires on the sheet: Function[5:0] = {EX[0], MEM, WriteBack};
  //   JumpAddress[25:0] = {Offset[16:0], EX, MEM, WriteBack}; BranchCode[4:0] = Offset[6:2];
  //   OpCode[5:0] = Offset[22:17]
endmodule
