// Logisim project IF ID.circ as structural Verilog: 1 circuit, main circuit main
module main (
  input  En,
  input  [31:0] IF_Inst,
  input  [31:0] IF_PC_4,
  input  CLK,
  input  Clear,
  output [31:0] ID_Inst,
  output [31:0] ID_PC_4
);

  Register #(.width(32), .Select("low")) Inst (.D(IF_Inst), .en(En), .Q(ID_Inst), .clk(CLK), .clr(Clear));
  Register #(.width(32), .Select("low")) PC (.D(IF_PC_4), .en(En), .Q(ID_PC_4), .clk(CLK), .clr(Clear));
endmodule
