// Logisim project RegisterFile.circ as structural Verilog: 1 circuit, main circuit Register
module Register (
  input  [31:0] in_1,
  input  [4:0] R_SELECTOR_1,
  input  [4:0] R_SELECTOR_2,
  output [31:0] OUTPUT_1,
  output [31:0] OUTPUT_2
);

  wire clock_1_out;
  wire [31:0] R0_q, R1_q, R2_q, R3_q, R4_q, R5_q, R6_q, R7_q, R8_q, R9_q, R10_q, R11_q, R12_q, R13_q, R14_q,
       R15_q, R16_q, R17_q, R18_q, R19_q, R20_q, R21_q, R22_q, R23_q, R24_q, R25_q, R26_q, R27_q, R28_q,
       R29_q, R30_q, R31_q;

  Register_part #(.width(32)) R0 (.Q(R0_q), .clk(clock_1_out));  // open: D, en, clr
  Register_part #(.width(32)) R8 (.Q(R8_q), .clk(clock_1_out));  // open: D, en, clr
  Register_part #(.width(32)) R16 (.Q(R16_q), .clk(clock_1_out));  // open: D, en, clr
  Register_part #(.width(32)) R24 (.Q(R24_q), .clk(clock_1_out));  // open: D, en, clr
  Register_part #(.width(32)) R1 (.Q(R1_q), .clk(clock_1_out));  // open: D, en, clr
  Register_part #(.width(32)) R9 (.Q(R9_q), .clk(clock_1_out));  // open: D, en, clr
  Register_part #(.width(32)) R17 (.Q(R17_q), .clk(clock_1_out));  // open: D, en, clr
  Register_part #(.width(32)) R25 (.Q(R25_q), .clk(clock_1_out));  // open: D, en, clr
  Register_part #(.width(32)) R2 (.Q(R2_q), .clk(clock_1_out));  // open: D, en, clr
  Register_part #(.width(32)) R10 (.Q(R10_q), .clk(clock_1_out));  // open: D, en, clr
  Register_part #(.width(32)) R18 (.Q(R18_q), .clk(clock_1_out));  // open: D, en, clr
  Register_part #(.width(32)) R26 (.Q(R26_q), .clk(clock_1_out));  // open: D, en, clr
  Register_part #(.width(32)) R3 (.Q(R3_q), .clk(clock_1_out));  // open: D, en, clr
  Register_part #(.width(32)) R11 (.Q(R11_q), .clk(clock_1_out));  // open: D, en, clr
  Register_part #(.width(32)) R19 (.Q(R19_q), .clk(clock_1_out));  // open: D, en, clr
  Register_part #(.width(32)) R27 (.Q(R27_q), .clk(clock_1_out));  // open: D, en, clr
  Clock clock_1 (.out(clock_1_out));
  Register_part #(.width(32)) R5 (.Q(R5_q), .clk(clock_1_out));  // open: D, en, clr
  Register_part #(.width(32)) R4 (.Q(R4_q), .clk(clock_1_out));  // open: D, en, clr
  Register_part #(.width(32)) R13 (.Q(R13_q), .clk(clock_1_out));  // open: D, en, clr
  Register_part #(.width(32)) R12 (.Q(R12_q), .clk(clock_1_out));  // open: D, en, clr
  Register_part #(.width(32)) R21 (.Q(R21_q), .clk(clock_1_out));  // open: D, en, clr
  Register_part #(.width(32)) R20 (.Q(R20_q), .clk(clock_1_out));  // open: D, en, clr
  Register_part #(.width(32)) R28 (.Q(R28_q), .clk(clock_1_out));  // open: D, en, clr
  Register_part #(.width(32)) R29 (.Q(R29_q), .clk(clock_1_out));  // open: D, en, clr
  Register_part #(.width(32)) R6 (.Q(R6_q), .clk(clock_1_out));  // open: D, en, clr
  Register_part #(.width(32)) R14 (.Q(R14_q), .clk(clock_1_out));  // open: D, en, clr
  Register_part #(.width(32)) R22 (.Q(R22_q), .clk(clock_1_out));  // open: D, en, clr
  Register_part #(.width(32)) R30 (.Q(R30_q), .clk(clock_1_out));  // open: D, en, clr
  Register_part #(.width(32)) R7 (.Q(R7_q), .clk(clock_1_out));  // open: D, en, clr
  Register_part #(.width(32)) R15 (.Q(R15_q), .clk(clock_1_out));  // open: D, en, clr
  Register_part #(.width(32)) R23 (.Q(R23_q), .clk(clock_1_out));  // open: D, en, clr
  Register_part #(.width(32)) R31 (.Q(R31_q), .clk(clock_1_out));  // open: D, en, clr
  Multiplexer #(.select(5), .width(32)) multiplexer_1 (
    .in0(R0_q), .in1(R1_q), .in2(R2_q), .in3(R3_q), .in4(R4_q), .in5(R5_q), .in6(R6_q), .in7(R7_q),
    .in8(R8_q), .in9(R9_q), .in10(R10_q), .in11(R11_q), .in12(R12_q), .in13(R13_q), .in14(R14_q),
    .in15(R15_q), .in16(R16_q), .in17(R17_q), .in18(R18_q), .in19(R19_q), .in20(R20_q), .in21(R21_q),
    .in22(R22_q), .in23(R23_q), .in24(R24_q), .in25(R25_q), .in26(R26_q), .in27(R27_q), .in28(R28_q),
    .in29(R29_q), .in30(R30_q), .in31(R31_q), .out(OUTPUT_1), .sel(R_SELECTOR_1), .en(clock_1_out));
  Multiplexer #(.select(5), .width(32)) multiplexer_2 (
    .in0(R0_q), .in1(R1_q), .in2(R2_q), .in3(R3_q), .in4(R4_q), .in5(R5_q), .in6(R6_q), .in7(R7_q),
    .in8(R8_q), .in9(R9_q), .in10(R10_q), .in11(R11_q), .in12(R12_q), .in13(R13_q), .in14(R14_q),
    .in15(R15_q), .in16(R16_q), .in17(R17_q), .in18(R18_q), .in19(R19_q), .in20(R20_q), .in21(R21_q),
    .in22(R22_q), .in23(R23_q), .in24(R24_q), .in25(R25_q), .in26(R26_q), .in27(R27_q), .in28(R28_q),
    .in29(R29_q), .in30(R30_q), .in31(R31_q), .out(OUTPUT_2), .sel(R_SELECTOR_2), .en(clock_1_out));
endmodule
